// Logisim project Calculadora2.circ as structural Verilog: 5 circuits, main circuit main
module main (
  input  [3:0] Numero_1,
  input  [1:0] Sinal,
  input  [3:0] Num_2
);

  wire button_1_out, calcular_1_out_5, calcular_1_out_6, calcular_1_out_7, calcular_1_out_8,
       calcular_1_out_9, calcular_1_out_10, calcular_1_out_11, calcular_1_out_12, calcular_1_out_13,
       centenas_1_s1, centenas_1_s2, centenas_1_s3, centenas_1_s4, centenas_1_s5, centenas_1_s6,
       centenas_1_s7, dezenas_1_s1, dezenas_1_s2, dezenas_1_s3, dezenas_1_s4, dezenas_1_s5, dezenas_1_s6,
       dezenas_1_s7, unidade_1_s1, unidade_1_s2, unidade_1_s3, unidade_1_s4, unidade_1_s5, unidade_1_s6,
       unidade_1_s7;

  Calcular calcular_1 (
    .in_2(Numero_1), .in_3(button_1_out), .in_4(Num_2), .in_1(Sinal), .out_13(calcular_1_out_13),
    .out_5(calcular_1_out_5), .out_6(calcular_1_out_6), .out_7(calcular_1_out_7), .out_8(calcular_1_out_8),
    .out_9(calcular_1_out_9), .out_10(calcular_1_out_10), .out_11(calcular_1_out_11),
    .out_12(calcular_1_out_12));
  Button button_1 (.out(button_1_out));
  Unidade unidade_1 (
    .Entrada8(calcular_1_out_12), .Entrada7(calcular_1_out_7), .Entrada6(calcular_1_out_10),
    .Entrada5(calcular_1_out_9), .Entrada4(calcular_1_out_8), .Entrada3(calcular_1_out_11),
    .Entrada2(calcular_1_out_6), .Entrada1(calcular_1_out_5), .S1(unidade_1_s1), .S2(unidade_1_s2),
    .S3(unidade_1_s3), .S4(unidade_1_s4), .S5(unidade_1_s5), .S6(unidade_1_s6), .S7(unidade_1_s7));
  Dezenas dezenas_1 (
    .E1(calcular_1_out_12), .E2(calcular_1_out_11), .E3(calcular_1_out_10), .E4(calcular_1_out_9),
    .E5(calcular_1_out_8), .E6(calcular_1_out_7), .E7(calcular_1_out_6), .S1(dezenas_1_s1),
    .E8(calcular_1_out_5), .S2(dezenas_1_s2), .S3(dezenas_1_s3), .S4(dezenas_1_s4), .S5(dezenas_1_s5),
    .S6(dezenas_1_s6), .S7(dezenas_1_s7));
  Centenas centenas_1 (
    .E1(calcular_1_out_12), .E2(calcular_1_out_11), .E3(calcular_1_out_10), .E4(calcular_1_out_9),
    .E5(calcular_1_out_8), .E6(calcular_1_out_7), .E7(calcular_1_out_6), .E8(calcular_1_out_5),
    .S1(centenas_1_s1), .S2(centenas_1_s2), .S3(centenas_1_s3), .S4(centenas_1_s4), .S5(centenas_1_s5),
    .S6(centenas_1_s6), .S7(centenas_1_s7));
  _7_Segment_Display u_7_segment_display_1 (
    .g(centenas_1_s1), .f(centenas_1_s2), .a(centenas_1_s3), .b(centenas_1_s4), .e(centenas_1_s5),
    .d(centenas_1_s6), .c(centenas_1_s7));  // open: dp
  _7_Segment_Display u_7_segment_display_2 (.g(calcular_1_out_13));  // open: f, a, b, e, d, c, dp
  _7_Segment_Display u_7_segment_display_3 (
    .g(dezenas_1_s1), .f(dezenas_1_s2), .a(dezenas_1_s3), .b(dezenas_1_s4), .e(dezenas_1_s5),
    .d(dezenas_1_s6), .c(dezenas_1_s7));  // open: dp
  _7_Segment_Display u_7_segment_display_4 (
    .g(unidade_1_s1), .f(unidade_1_s2), .a(unidade_1_s3), .b(unidade_1_s4), .e(unidade_1_s5),
    .d(unidade_1_s6), .c(unidade_1_s7));  // open: dp

  // Notes on the sheet:
  //   Sinais
  //   Soma 00
  //   Subtração 01
  //   Multiplicação 10
  //   Divisão 11
  //   Bit de sinal
endmodule

module Calcular (
  input  [1:0] in_1,
  input  [3:0] in_2,
  input  in_3,
  input  [3:0] in_4,
  output out_5,
  output out_6,
  output out_7,
  output out_8,
  output out_9,
  output out_10,
  output out_11,
  output out_12,
  output out_13
);

  wire comparator_1_lt, comparator_2_eq, comparator_3_eq, comparator_3_gt, comparator_3_lt;
  wire [1:0] register_1_q;
  wire [7:0] adder_1_out, bit_extender_1_out, bit_extender_2_out, divider_1_out, multiplexer_1_out,
       multiplier_1_out, register_2_q, register_3_q, subtractor_1_out, subtractor_2_out, transmission_1_p4,
       transmission_2_p4, transmission_3_p4, transmission_4_p4;

  Comparator comparator_1 (.a(register_2_q), .b(register_3_q), .lt(comparator_1_lt));  // open: gt, eq
  Register #(.width(2)) register_1 (.D(in_1), .Q(register_1_q), .clk(in_3));  // open: en, clr
  Register register_2 (.D(bit_extender_1_out), .Q(register_2_q), .clk(in_3));  // open: en, clr
  assign bit_extender_1_out = {{4{1'b0}}, in_2};  // Bit_Extender bit_extender_1
  assign bit_extender_2_out = {{4{1'b0}}, in_4};  // Bit_Extender bit_extender_2
  Register register_3 (.D(bit_extender_2_out), .Q(register_3_q), .clk(in_3));  // open: en, clr
  Comparator #(.width(2)) comparator_2 (.a(2'b01), .b(register_1_q), .eq(comparator_2_eq));  // open: gt, lt
  and and_1 (out_13, comparator_1_lt, comparator_2_eq);
  Subtractor subtractor_1 (.a(register_2_q), .b(register_3_q), .out(subtractor_1_out));  // open: bin, bout
  Subtractor subtractor_2 (.a(register_3_q), .b(register_2_q), .out(subtractor_2_out));  // open: bin, bout
  Multiplexer #(.width(8), .enable("false")) multiplexer_1 (
    .in0(subtractor_1_out), .in1(subtractor_2_out), .out(multiplexer_1_out), .sel(out_13));
  Comparator #(.width(1)) comparator_3 (
    .a(register_1_q[0]), .b(register_1_q[1]), .gt(comparator_3_gt), .eq(comparator_3_eq), .lt(comparator_3_lt));
  Adder adder_1 (.a(register_2_q), .b(register_3_q), .out(adder_1_out));  // open: cin, cout
  Multiplier multiplier_1 (.a(register_2_q), .b(register_3_q), .out(multiplier_1_out));  // open: cin, cout
  Divider divider_1 (.a(register_2_q), .b(register_3_q), .out(divider_1_out));  // open: upper, rem
  // Transmission_Gate #(.gate("br"), .width(8)) transmission_1: pin names not known; wires that end beside it: multiplexer_1_out, comparator_3_lt, 1'b0, transmission_1_p4
  // Transmission_Gate #(.gate("br"), .width(8)) transmission_2: pin names not known; wires that end beside it: adder_1_out, comparator_3_eq, 1'b0, transmission_2_p4
  // Transmission_Gate #(.gate("br"), .width(8)) transmission_3: pin names not known; wires that end beside it: multiplier_1_out, comparator_3_gt, 1'b0, transmission_3_p4
  // Transmission_Gate #(.gate("br"), .width(8)) transmission_4: pin names not known; wires that end beside it: divider_1_out, comparator_3_eq, 1'b0, transmission_4_p4
  Multiplexer #(.select(2), .width(8), .enable("false")) multiplexer_2 (
    .in0(transmission_2_p4), .in1(transmission_1_p4), .in2(transmission_3_p4), .in3(transmission_4_p4),
    .out({out_12, out_11, out_10, out_9, out_8, out_7, out_6, out_5}), .sel(register_1_q));
endmodule
module Unidade (
  input  Entrada8,
  input  Entrada7,
  input  Entrada6,
  input  Entrada5,
  input  Entrada4,
  input  Entrada3,
  input  Entrada2,
  input  Entrada1,
  output S1,
  output S2,
  output S3,
  output S4,
  output S5,
  output S6,
  output S7
);

  wire and_1_out, and_2_out, and_3_out, and_4_out, and_5_out, and_6_out, and_7_out, and_8_out, and_9_out,
       and_10_out, and_11_out, and_12_out, and_13_out, and_14_out, and_15_out, and_16_out, and_17_out,
       and_18_out, and_19_out, and_20_out, and_21_out, and_22_out, and_23_out, and_24_out, and_25_out,
       and_26_out, and_27_out, and_28_out, and_29_out, and_30_out, and_31_out, and_32_out, and_33_out,
       and_34_out, and_35_out, and_36_out, and_37_out, and_38_out, and_39_out, and_40_out, and_41_out,
       and_42_out, and_43_out, and_44_out, and_45_out, and_46_out, and_47_out, and_48_out, and_49_out,
       and_50_out, and_51_out, and_52_out, and_53_out, and_54_out, and_55_out, and_56_out, and_57_out,
       and_58_out, and_59_out, and_60_out, and_61_out, and_62_out, and_63_out, and_64_out, and_65_out,
       and_66_out, and_67_out, and_68_out, and_69_out, and_70_out, and_71_out, and_72_out, and_73_out,
       and_74_out, and_75_out, and_76_out, and_77_out, and_78_out, and_79_out, and_80_out, and_81_out,
       and_82_out, and_83_out, and_84_out, and_85_out, and_86_out, and_87_out, and_88_out, and_89_out,
       and_90_out, and_91_out, and_92_out, and_93_out, and_94_out, and_95_out, and_96_out, and_97_out,
       and_98_out, and_99_out, and_100_out, and_101_out, and_102_out, and_103_out, and_104_out, and_105_out,
       and_106_out, and_107_out, and_108_out, and_109_out, and_110_out, and_111_out, and_112_out,
       and_113_out, and_114_out, and_115_out, and_116_out, and_117_out, and_118_out, and_119_out,
       and_120_out, and_121_out, and_122_out, and_123_out, and_124_out, and_125_out, and_126_out,
       and_127_out, and_128_out, and_129_out, and_130_out, and_131_out, and_132_out, and_133_out,
       and_134_out, and_135_out, and_136_out, and_137_out, and_138_out, and_139_out, and_140_out,
       and_141_out, and_142_out, and_143_out, and_144_out, and_145_out, and_146_out, and_147_out,
       and_148_out, and_149_out, and_150_out, and_151_out, and_152_out, and_153_out, and_154_out,
       and_155_out, and_156_out, and_157_out, and_158_out, and_159_out, and_160_out, and_161_out,
       and_162_out, and_163_out, and_164_out, and_165_out, and_166_out, and_167_out, and_168_out,
       and_169_out, and_170_out, and_171_out, and_172_out, and_173_out, and_174_out, and_175_out,
       and_176_out, and_177_out, and_178_out, and_179_out, and_180_out, and_181_out, and_182_out,
       and_183_out, and_184_out, and_185_out, and_186_out, and_187_out, and_188_out, and_189_out,
       and_190_out, and_191_out, and_192_out, and_193_out, and_194_out, and_195_out, and_196_out,
       and_197_out, and_198_out, and_199_out, and_200_out, and_201_out, and_202_out, and_203_out,
       and_204_out, and_205_out, and_206_out, and_207_out, and_208_out, and_209_out, and_210_out,
       and_211_out, and_212_out, and_213_out, and_214_out, and_215_out, and_216_out, and_217_out,
       and_218_out, and_219_out, and_220_out, and_221_out, and_222_out, and_223_out, and_224_out,
       and_225_out, and_226_out, and_227_out, and_228_out, and_229_out, and_230_out, and_231_out,
       and_232_out, and_233_out, and_234_out, and_235_out, and_236_out, and_237_out, and_238_out,
       and_239_out, and_240_out, and_241_out, and_242_out, and_243_out, and_244_out, and_245_out,
       and_246_out, and_247_out, and_248_out, and_249_out, and_250_out, and_251_out, and_252_out,
       and_253_out, and_254_out, and_255_out, and_256_out, and_257_out, and_258_out, and_259_out,
       and_260_out, and_261_out, and_262_out, and_263_out, and_264_out, and_265_out, and_266_out,
       and_267_out, and_268_out, and_269_out, and_270_out, and_271_out, and_272_out, and_273_out,
       and_274_out, and_275_out, and_276_out, and_277_out, and_278_out, and_279_out, and_280_out,
       and_281_out, and_282_out, and_283_out, and_284_out, and_285_out, and_286_out, and_287_out,
       and_288_out, and_289_out, and_290_out, and_291_out, and_292_out, and_293_out, and_294_out,
       and_295_out, and_296_out, and_297_out, and_298_out, and_299_out, and_300_out, and_301_out,
       and_302_out, and_303_out, and_304_out, and_305_out, and_306_out, and_307_out, and_308_out,
       and_309_out, and_310_out, and_311_out, and_312_out, and_313_out, and_314_out, and_315_out,
       and_316_out, and_317_out, and_318_out, and_319_out, and_320_out, and_321_out, and_322_out,
       and_323_out, and_324_out, and_325_out, and_326_out, and_327_out, and_328_out, and_329_out,
       and_330_out, and_331_out, and_332_out, and_333_out, and_334_out, and_335_out, and_336_out,
       and_337_out, and_338_out, and_339_out, and_340_out, and_341_out, and_342_out, and_343_out,
       and_344_out, and_345_out, and_346_out, and_347_out, and_348_out, and_349_out, and_350_out,
       and_351_out, and_352_out, and_353_out, and_354_out, and_355_out, and_356_out, and_357_out,
       and_358_out, and_359_out, and_360_out, and_361_out, and_362_out, and_363_out, and_364_out,
       and_365_out, and_366_out, and_367_out, and_368_out, and_369_out, and_370_out, and_371_out,
       and_372_out, and_373_out, and_374_out, and_375_out, not_1_out, not_2_out, not_3_out, not_4_out,
       not_5_out, not_6_out, not_7_out, not_8_out, not_9_out, not_10_out, not_11_out, not_12_out, not_13_out,
       not_14_out, not_15_out, not_16_out, not_17_out, not_18_out, not_19_out, not_20_out, not_21_out,
       not_22_out, not_23_out, not_24_out, not_25_out, not_26_out, not_27_out, not_28_out, not_29_out,
       not_30_out, not_31_out, not_32_out, not_33_out, not_34_out, not_35_out, not_36_out, not_37_out,
       not_38_out, not_39_out, not_40_out, not_41_out, not_42_out, not_43_out, not_44_out, not_45_out,
       not_46_out, not_47_out, not_48_out, not_49_out, not_50_out, not_51_out, not_52_out, not_53_out,
       not_54_out, not_55_out, not_56_out, not_57_out, not_58_out, not_59_out, not_60_out, not_61_out,
       not_62_out, not_63_out, not_64_out, not_65_out, not_66_out, not_67_out, not_68_out, not_69_out,
       not_70_out, not_71_out, not_72_out, not_73_out, not_74_out, not_75_out, not_76_out, not_77_out,
       not_78_out, not_79_out, not_80_out, not_81_out, not_82_out, not_83_out, not_84_out, not_85_out,
       not_86_out, not_87_out, not_88_out, not_89_out, not_90_out, not_91_out, not_92_out, not_93_out,
       not_94_out, not_95_out, not_96_out, not_97_out, not_98_out, not_99_out, not_100_out, not_101_out,
       not_102_out, not_103_out, not_104_out, not_105_out, not_106_out, not_107_out, not_108_out,
       not_109_out, not_110_out, not_111_out, not_112_out, not_113_out, not_114_out, not_115_out,
       not_116_out, not_117_out, not_118_out, not_119_out, not_120_out, not_121_out, not_122_out,
       not_123_out, not_124_out, not_125_out, not_126_out, not_127_out, not_128_out, not_129_out,
       not_130_out, not_131_out, not_132_out, not_133_out, not_134_out, not_135_out, not_136_out,
       not_137_out, not_138_out, not_139_out, not_140_out, not_141_out, not_142_out, not_143_out,
       not_144_out, not_145_out, not_146_out, not_147_out, not_148_out, not_149_out, not_150_out,
       not_151_out, not_152_out, not_153_out, not_154_out, not_155_out, not_156_out, not_157_out,
       not_158_out, not_159_out, not_160_out, not_161_out, not_162_out, not_163_out, not_164_out,
       not_165_out, not_166_out, not_167_out, not_168_out, not_169_out, not_170_out, not_171_out,
       not_172_out, not_173_out, not_174_out, not_175_out, not_176_out, not_177_out, not_178_out,
       not_179_out, not_180_out, not_181_out, not_182_out, not_183_out, not_184_out, not_185_out,
       not_186_out, not_187_out, not_188_out, not_189_out, not_190_out, not_191_out, not_192_out,
       not_193_out, not_194_out, not_195_out, not_196_out, not_197_out, not_198_out, not_199_out,
       not_200_out, not_201_out, not_202_out, not_203_out, not_204_out, not_205_out, not_206_out,
       not_207_out, not_208_out, not_209_out, not_210_out, not_211_out, not_212_out, not_213_out,
       not_214_out, not_215_out, not_216_out, not_217_out, not_218_out, not_219_out, not_220_out,
       not_221_out, not_222_out, not_223_out, not_224_out, not_225_out, not_226_out, not_227_out,
       not_228_out, not_229_out, not_230_out, not_231_out, not_232_out, not_233_out, not_234_out,
       not_235_out, not_236_out, not_237_out, not_238_out, not_239_out, not_240_out, not_241_out,
       not_242_out, not_243_out, not_244_out, not_245_out, not_246_out, not_247_out, not_248_out,
       not_249_out, not_250_out, not_251_out, not_252_out, not_253_out, not_254_out, not_255_out,
       not_256_out, not_257_out, not_258_out, not_259_out, not_260_out, not_261_out, not_262_out,
       not_263_out, not_264_out, not_265_out, not_266_out, not_267_out, not_268_out, not_269_out,
       not_270_out, not_271_out, not_272_out, not_273_out, not_274_out, not_275_out, not_276_out,
       not_277_out, not_278_out, not_279_out, not_280_out, not_281_out, not_282_out, not_283_out,
       not_284_out, not_285_out, not_286_out, not_287_out, not_288_out, not_289_out, not_290_out,
       not_291_out, not_292_out, not_293_out, not_294_out, not_295_out, not_296_out, not_297_out,
       not_298_out, not_299_out, not_300_out, not_301_out, not_302_out, not_303_out, not_304_out,
       not_305_out, not_306_out, not_307_out, not_308_out, not_309_out, not_310_out, not_311_out,
       not_312_out, not_313_out, not_314_out, not_315_out, not_316_out, not_317_out, not_318_out,
       not_319_out, not_320_out, not_321_out, not_322_out, not_323_out, not_324_out, not_325_out,
       not_326_out, not_327_out, not_328_out, not_329_out, not_330_out, not_331_out, not_332_out,
       not_333_out, not_334_out, not_335_out, not_336_out, not_337_out, not_338_out, not_339_out,
       not_340_out, not_341_out, not_342_out, not_343_out, not_344_out, not_345_out, not_346_out,
       not_347_out, not_348_out, not_349_out, not_350_out, not_351_out, not_352_out, not_353_out,
       not_354_out, not_355_out, not_356_out, not_357_out, not_358_out, not_359_out, not_360_out,
       not_361_out, not_362_out, not_363_out, not_364_out, not_365_out, not_366_out, not_367_out,
       not_368_out, not_369_out, not_370_out, not_371_out, not_372_out, not_373_out, not_374_out,
       not_375_out, not_376_out, not_377_out, not_378_out, not_379_out, not_380_out, not_381_out,
       not_382_out, not_383_out, not_384_out, not_385_out, not_386_out, not_387_out, not_388_out,
       not_389_out, not_390_out, not_391_out, not_392_out, not_393_out, not_394_out, not_395_out,
       not_396_out, not_397_out, not_398_out, not_399_out, not_400_out, not_401_out, not_402_out,
       not_403_out, not_404_out, not_405_out, not_406_out, not_407_out, not_408_out, not_409_out,
       not_410_out, not_411_out, not_412_out, not_413_out, not_414_out, not_415_out, not_416_out,
       not_417_out, not_418_out, not_419_out, not_420_out, not_421_out, not_422_out, not_423_out,
       not_424_out, not_425_out, not_426_out, not_427_out, not_428_out, not_429_out, not_430_out,
       not_431_out, not_432_out, not_433_out, not_434_out, not_435_out, not_436_out, not_437_out,
       not_438_out, not_439_out, not_440_out, not_441_out, not_442_out, not_443_out, not_444_out,
       not_445_out, not_446_out, not_447_out, not_448_out, not_449_out, not_450_out, not_451_out,
       not_452_out, not_453_out, not_454_out, not_455_out, not_456_out, not_457_out, not_458_out,
       not_459_out, not_460_out, not_461_out, not_462_out, not_463_out, not_464_out, not_465_out,
       not_466_out, not_467_out, not_468_out, not_469_out, not_470_out, not_471_out, not_472_out,
       not_473_out, not_474_out, not_475_out, not_476_out, not_477_out, not_478_out, not_479_out,
       not_480_out, not_481_out, not_482_out, not_483_out, not_484_out, not_485_out, not_486_out,
       not_487_out, not_488_out, not_489_out, not_490_out, not_491_out, not_492_out, not_493_out,
       not_494_out, not_495_out, not_496_out, not_497_out, not_498_out, not_499_out, not_500_out,
       not_501_out, not_502_out, not_503_out, not_504_out, not_505_out, not_506_out, not_507_out,
       not_508_out, not_509_out, not_510_out, not_511_out, not_512_out, not_513_out, not_514_out,
       not_515_out, not_516_out, not_517_out, not_518_out, not_519_out, not_520_out, not_521_out,
       not_522_out, not_523_out, not_524_out, not_525_out, not_526_out, not_527_out, not_528_out,
       not_529_out, not_530_out, not_531_out, not_532_out, not_533_out, not_534_out, not_535_out,
       not_536_out, not_537_out, not_538_out, not_539_out, not_540_out, not_541_out, not_542_out,
       not_543_out, not_544_out, not_545_out, not_546_out, not_547_out, not_548_out, not_549_out,
       not_550_out, not_551_out, not_552_out, not_553_out, not_554_out, not_555_out, not_556_out,
       not_557_out, not_558_out, not_559_out, not_560_out, not_561_out, not_562_out, not_563_out,
       not_564_out, not_565_out, not_566_out, not_567_out, not_568_out, not_569_out, not_570_out,
       not_571_out, not_572_out, not_573_out, not_574_out, not_575_out, not_576_out, not_577_out,
       not_578_out, not_579_out, not_580_out, not_581_out, not_582_out, not_583_out, not_584_out,
       not_585_out, not_586_out, not_587_out, not_588_out, not_589_out, not_590_out, not_591_out,
       not_592_out, not_593_out, not_594_out, not_595_out, not_596_out, not_597_out, not_598_out,
       not_599_out, not_600_out, not_601_out, not_602_out, not_603_out, not_604_out, not_605_out,
       not_606_out, not_607_out, not_608_out, not_609_out, not_610_out, not_611_out, not_612_out,
       not_613_out, not_614_out, not_615_out, not_616_out, not_617_out, not_618_out, not_619_out,
       not_620_out, not_621_out, not_622_out, not_623_out, not_624_out, not_625_out, not_626_out,
       not_627_out, not_628_out, not_629_out, not_630_out, not_631_out, not_632_out, not_633_out,
       not_634_out, not_635_out, not_636_out, not_637_out, not_638_out, not_639_out, not_640_out,
       not_641_out, not_642_out, not_643_out, not_644_out, not_645_out, not_646_out, not_647_out,
       not_648_out, not_649_out, not_650_out, not_651_out, not_652_out, not_653_out, not_654_out,
       not_655_out, not_656_out, not_657_out, not_658_out, not_659_out, not_660_out, not_661_out,
       not_662_out, not_663_out, not_664_out, not_665_out, not_666_out, not_667_out, not_668_out,
       not_669_out, not_670_out, not_671_out, not_672_out, not_673_out, not_674_out, not_675_out,
       not_676_out, not_677_out, not_678_out, not_679_out, not_680_out, not_681_out, not_682_out,
       not_683_out, not_684_out, not_685_out, not_686_out, not_687_out, not_688_out, not_689_out,
       not_690_out, not_691_out, not_692_out, not_693_out, not_694_out, not_695_out, not_696_out,
       not_697_out, not_698_out, not_699_out, not_700_out, not_701_out, not_702_out, not_703_out,
       not_704_out, not_705_out, not_706_out, not_707_out, not_708_out, not_709_out, not_710_out,
       not_711_out, not_712_out, not_713_out, not_714_out, not_715_out, not_716_out, not_717_out,
       not_718_out, not_719_out, not_720_out, not_721_out, not_722_out, not_723_out, not_724_out,
       not_725_out, not_726_out, not_727_out, not_728_out, not_729_out, not_730_out, not_731_out,
       not_732_out, not_733_out, not_734_out, not_735_out, not_736_out, not_737_out, not_738_out,
       not_739_out, not_740_out, not_741_out, not_742_out, not_743_out, not_744_out, not_745_out,
       not_746_out, not_747_out, not_748_out, not_749_out, not_750_out, not_751_out, not_752_out,
       not_753_out, not_754_out, not_755_out, not_756_out, not_757_out, not_758_out, not_759_out,
       not_760_out, not_761_out, not_762_out, not_763_out, not_764_out, not_765_out, not_766_out,
       not_767_out, not_768_out, not_769_out, not_770_out, not_771_out, not_772_out, not_773_out,
       not_774_out, not_775_out, not_776_out, not_777_out, not_778_out, not_779_out, not_780_out,
       not_781_out, not_782_out, not_783_out, not_784_out, not_785_out, not_786_out, not_787_out,
       not_788_out, not_789_out, not_790_out, not_791_out, not_792_out, not_793_out, not_794_out,
       not_795_out, not_796_out, not_797_out, not_798_out, not_799_out, not_800_out, not_801_out,
       not_802_out, not_803_out, not_804_out, not_805_out, not_806_out, not_807_out, not_808_out,
       not_809_out, not_810_out, not_811_out, not_812_out, not_813_out, not_814_out, not_815_out,
       not_816_out, not_817_out, not_818_out, not_819_out, not_820_out, not_821_out, not_822_out,
       not_823_out, not_824_out, not_825_out, not_826_out, not_827_out, not_828_out, not_829_out,
       not_830_out, not_831_out, not_832_out, not_833_out, not_834_out, not_835_out, not_836_out,
       not_837_out, not_838_out, not_839_out, not_840_out, not_841_out, not_842_out, not_843_out,
       not_844_out, not_845_out, not_846_out, not_847_out, not_848_out, not_849_out, not_850_out,
       not_851_out, not_852_out, not_853_out, not_854_out, not_855_out, not_856_out, not_857_out,
       not_858_out, not_859_out, not_860_out, not_861_out, not_862_out, not_863_out, not_864_out,
       not_865_out, not_866_out, not_867_out, not_868_out, not_869_out, not_870_out, not_871_out,
       not_872_out, not_873_out, not_874_out, not_875_out, not_876_out, not_877_out, not_878_out,
       not_879_out, not_880_out, not_881_out, not_882_out, not_883_out, not_884_out, not_885_out,
       not_886_out, not_887_out, not_888_out, not_889_out, not_890_out, not_891_out, not_892_out,
       not_893_out, not_894_out, not_895_out, not_896_out, not_897_out, not_898_out, not_899_out,
       not_900_out, not_901_out, not_902_out, not_903_out, not_904_out, not_905_out, not_906_out,
       not_907_out, not_908_out, not_909_out, not_910_out, not_911_out, not_912_out, not_913_out,
       not_914_out, not_915_out, not_916_out, not_917_out, not_918_out, not_919_out, not_920_out,
       not_921_out, not_922_out, not_923_out, not_924_out, not_925_out, not_926_out, not_927_out,
       not_928_out, not_929_out, not_930_out, not_931_out, not_932_out, not_933_out, not_934_out,
       not_935_out, not_936_out, not_937_out, not_938_out, not_939_out, not_940_out, not_941_out,
       not_942_out, not_943_out, not_944_out, not_945_out, not_946_out, not_947_out, not_948_out,
       not_949_out, not_950_out, not_951_out, not_952_out, not_953_out, not_954_out, not_955_out,
       not_956_out, not_957_out, not_958_out, not_959_out, not_960_out, not_961_out, not_962_out,
       not_963_out, not_964_out, not_965_out, not_966_out, not_967_out, not_968_out, not_969_out,
       not_970_out, not_971_out, not_972_out, not_973_out, not_974_out, not_975_out, not_976_out,
       not_977_out, not_978_out, not_979_out, not_980_out, not_981_out, not_982_out, not_983_out,
       not_984_out, not_985_out, not_986_out, not_987_out, not_988_out, not_989_out, not_990_out,
       not_991_out, not_992_out, not_993_out, not_994_out, not_995_out, not_996_out, not_997_out,
       not_998_out, not_999_out, not_1000_out, not_1001_out, not_1002_out, not_1003_out, not_1004_out,
       not_1005_out, not_1006_out, not_1007_out, not_1008_out, not_1009_out, not_1010_out, not_1011_out,
       not_1012_out, not_1013_out, not_1014_out, not_1015_out, not_1016_out, not_1017_out, not_1018_out,
       not_1019_out, not_1020_out, not_1021_out, not_1022_out, not_1023_out, not_1024_out, not_1025_out,
       not_1026_out, not_1027_out, not_1028_out, not_1029_out, not_1030_out, not_1031_out, not_1032_out,
       not_1033_out, not_1034_out, not_1035_out, not_1036_out, not_1037_out, not_1038_out, not_1039_out,
       not_1040_out, not_1041_out, not_1042_out, not_1043_out, not_1044_out, not_1045_out, not_1046_out,
       not_1047_out, not_1048_out, not_1049_out, not_1050_out, not_1051_out, not_1052_out, not_1053_out,
       not_1054_out, not_1055_out, not_1056_out, not_1057_out, not_1058_out, not_1059_out, not_1060_out,
       not_1061_out, not_1062_out, not_1063_out, not_1064_out, not_1065_out, not_1066_out, not_1067_out,
       not_1068_out, not_1069_out, not_1070_out, not_1071_out, not_1072_out, not_1073_out, not_1074_out,
       not_1075_out, not_1076_out, not_1077_out, not_1078_out, not_1079_out, not_1080_out, not_1081_out,
       not_1082_out, not_1083_out, not_1084_out, not_1085_out, not_1086_out, not_1087_out, not_1088_out,
       not_1089_out, not_1090_out, not_1091_out, not_1092_out, not_1093_out, not_1094_out, not_1095_out,
       not_1096_out, not_1097_out, not_1098_out, not_1099_out, not_1100_out, not_1101_out, not_1102_out,
       not_1103_out, not_1104_out, not_1105_out, not_1106_out, not_1107_out, not_1108_out, not_1109_out,
       not_1110_out, not_1111_out, not_1112_out, not_1113_out, not_1114_out, not_1115_out, not_1116_out,
       not_1117_out, not_1118_out, not_1119_out, not_1120_out, not_1121_out, not_1122_out, not_1123_out,
       not_1124_out, not_1125_out, not_1126_out, not_1127_out, not_1128_out, not_1129_out, not_1130_out,
       not_1131_out, not_1132_out, not_1133_out, not_1134_out, not_1135_out, not_1136_out, not_1137_out,
       not_1138_out, not_1139_out, not_1140_out, not_1141_out, not_1142_out, not_1143_out, not_1144_out,
       not_1145_out, not_1146_out, not_1147_out, not_1148_out, not_1149_out, not_1150_out, not_1151_out,
       not_1152_out, or_1_out, or_2_out, or_3_out, or_4_out, or_5_out, or_6_out, or_7_out, or_8_out,
       or_9_out, or_10_out, or_12_out, or_13_out, or_14_out;

  not not_1 (not_1_out, Entrada8);
  not not_2 (not_2_out, Entrada7);
  not not_3 (not_3_out, Entrada6);
  not not_4 (not_4_out, Entrada4);
  not not_5 (not_5_out, Entrada3);
  not not_6 (not_6_out, Entrada8);
  not not_7 (not_7_out, Entrada7);
  not not_8 (not_8_out, Entrada6);
  not not_9 (not_9_out, Entrada5);
  not not_10 (not_10_out, Entrada2);
  not not_11 (not_11_out, Entrada8);
  not not_12 (not_12_out, Entrada7);
  not not_13 (not_13_out, Entrada5);
  not not_14 (not_14_out, Entrada1);
  not not_15 (not_15_out, Entrada7);
  not not_16 (not_16_out, Entrada5);
  not not_17 (not_17_out, Entrada4);
  not not_18 (not_18_out, Entrada1);
  not not_19 (not_19_out, Entrada8);
  not not_20 (not_20_out, Entrada7);
  not not_21 (not_21_out, Entrada6);
  not not_22 (not_22_out, Entrada2);
  not not_23 (not_23_out, Entrada8);
  not not_24 (not_24_out, Entrada6);
  not not_25 (not_25_out, Entrada3);
  not not_26 (not_26_out, Entrada2);
  not not_27 (not_27_out, Entrada8);
  not not_28 (not_28_out, Entrada7);
  not not_29 (not_29_out, Entrada6);
  not not_30 (not_30_out, Entrada5);
  not not_31 (not_31_out, Entrada8);
  not not_32 (not_32_out, Entrada7);
  not not_33 (not_33_out, Entrada5);
  not not_34 (not_34_out, Entrada2);
  not not_35 (not_35_out, Entrada7);
  not not_36 (not_36_out, Entrada6);
  not not_37 (not_37_out, Entrada3);
  not not_38 (not_38_out, Entrada1);
  not not_39 (not_39_out, Entrada7);
  not not_40 (not_40_out, Entrada3);
  not not_41 (not_41_out, Entrada2);
  not not_42 (not_42_out, Entrada1);
  not not_43 (not_43_out, Entrada8);
  not not_44 (not_44_out, Entrada7);
  not not_45 (not_45_out, Entrada6);
  not not_46 (not_46_out, Entrada4);
  not not_47 (not_47_out, Entrada8);
  not not_48 (not_48_out, Entrada6);
  not not_49 (not_49_out, Entrada4);
  not not_50 (not_50_out, Entrada3);
  not not_51 (not_51_out, Entrada8);
  not not_52 (not_52_out, Entrada7);
  not not_53 (not_53_out, Entrada4);
  not not_54 (not_54_out, Entrada3);
  not not_55 (not_55_out, Entrada2);
  not not_56 (not_56_out, Entrada8);
  not not_57 (not_57_out, Entrada5);
  not not_58 (not_58_out, Entrada4);
  not not_59 (not_59_out, Entrada8);
  not not_60 (not_60_out, Entrada7);
  not not_61 (not_61_out, Entrada3);
  not not_62 (not_62_out, Entrada8);
  not not_63 (not_63_out, Entrada7);
  not not_64 (not_64_out, Entrada4);
  not not_65 (not_65_out, Entrada8);
  not not_66 (not_66_out, Entrada7);
  not not_67 (not_67_out, Entrada8);
  not not_68 (not_68_out, Entrada6);
  not not_69 (not_69_out, Entrada5);
  not not_70 (not_70_out, Entrada4);
  not not_71 (not_71_out, Entrada2);
  not not_72 (not_72_out, Entrada8);
  not not_73 (not_73_out, Entrada5);
  not not_74 (not_74_out, Entrada3);
  not not_75 (not_75_out, Entrada1);
  not not_76 (not_76_out, Entrada6);
  not not_77 (not_77_out, Entrada5);
  not not_78 (not_78_out, Entrada2);
  not not_79 (not_79_out, Entrada1);
  not not_80 (not_80_out, Entrada8);
  not not_81 (not_81_out, Entrada6);
  not not_82 (not_82_out, Entrada5);
  not not_83 (not_83_out, Entrada8);
  not not_84 (not_84_out, Entrada6);
  not not_85 (not_85_out, Entrada2);
  not not_86 (not_86_out, Entrada8);
  not not_87 (not_87_out, Entrada1);
  not not_88 (not_88_out, Entrada4);
  not not_89 (not_89_out, Entrada1);
  not not_90 (not_90_out, Entrada8);
  not not_91 (not_91_out, Entrada6);
  not not_92 (not_92_out, Entrada5);
  not not_93 (not_93_out, Entrada3);
  not not_94 (not_94_out, Entrada1);
  not not_95 (not_95_out, Entrada8);
  not not_96 (not_96_out, Entrada4);
  not not_97 (not_97_out, Entrada8);
  not not_98 (not_98_out, Entrada5);
  not not_99 (not_99_out, Entrada2);
  not not_100 (not_100_out, Entrada8);
  not not_101 (not_101_out, Entrada2);
  not not_102 (not_102_out, Entrada8);
  not not_103 (not_103_out, Entrada4);
  not not_104 (not_104_out, Entrada3);
  not not_105 (not_105_out, Entrada8);
  not not_106 (not_106_out, Entrada3);
  not not_107 (not_107_out, Entrada7);
  not not_108 (not_108_out, Entrada6);
  not not_109 (not_109_out, Entrada4);
  not not_110 (not_110_out, Entrada2);
  not not_111 (not_111_out, Entrada7);
  not not_112 (not_112_out, Entrada6);
  not not_113 (not_113_out, Entrada3);
  not not_114 (not_114_out, Entrada2);
  not not_115 (not_115_out, Entrada1);
  not not_116 (not_116_out, Entrada6);
  not not_117 (not_117_out, Entrada4);
  not not_118 (not_118_out, Entrada3);
  not not_119 (not_119_out, Entrada2);
  not not_120 (not_120_out, Entrada7);
  not not_121 (not_121_out, Entrada6);
  not not_122 (not_122_out, Entrada5);
  not not_123 (not_123_out, Entrada4);
  not not_124 (not_124_out, Entrada7);
  not not_125 (not_125_out, Entrada6);
  not not_126 (not_126_out, Entrada6);
  not not_127 (not_127_out, Entrada3);
  not not_128 (not_128_out, Entrada7);
  not not_129 (not_129_out, Entrada6);
  not not_130 (not_130_out, Entrada3);
  not not_131 (not_131_out, Entrada2);
  not not_132 (not_132_out, Entrada7);
  not not_133 (not_133_out, Entrada6);
  not not_134 (not_134_out, Entrada2);
  not not_135 (not_135_out, Entrada1);
  not not_136 (not_136_out, Entrada7);
  not not_137 (not_137_out, Entrada3);
  not not_138 (not_138_out, Entrada1);
  not not_139 (not_139_out, Entrada6);
  not not_140 (not_140_out, Entrada3);
  not not_141 (not_141_out, Entrada2);
  not not_142 (not_142_out, Entrada1);
  not not_143 (not_143_out, Entrada7);
  not not_144 (not_144_out, Entrada4);
  not not_145 (not_145_out, Entrada3);
  not not_146 (not_146_out, Entrada5);
  not not_147 (not_147_out, Entrada4);
  not not_148 (not_148_out, Entrada2);
  not not_149 (not_149_out, Entrada7);
  not not_150 (not_150_out, Entrada2);
  not not_151 (not_151_out, Entrada5);
  not not_152 (not_152_out, Entrada7);
  not not_153 (not_153_out, Entrada4);
  not not_154 (not_154_out, Entrada4);
  not not_155 (not_155_out, Entrada3);
  not not_156 (not_156_out, Entrada2);
  not not_157 (not_157_out, Entrada6);
  not not_158 (not_158_out, Entrada5);
  not not_159 (not_159_out, Entrada4);
  not not_160 (not_160_out, Entrada6);
  not not_161 (not_161_out, Entrada5);
  not not_162 (not_162_out, Entrada2);
  not not_163 (not_163_out, Entrada5);
  not not_164 (not_164_out, Entrada1);
  not not_165 (not_165_out, Entrada6);
  not not_166 (not_166_out, Entrada4);
  not not_167 (not_167_out, Entrada5);
  not not_168 (not_168_out, Entrada3);
  not not_169 (not_169_out, Entrada2);
  not not_170 (not_170_out, Entrada4);
  not not_171 (not_171_out, Entrada2);
  not not_172 (not_172_out, Entrada5);
  not not_173 (not_173_out, Entrada3);
  not not_174 (not_174_out, Entrada8);
  not not_175 (not_175_out, Entrada6);
  not not_176 (not_176_out, Entrada4);
  not not_177 (not_177_out, Entrada2);
  not not_178 (not_178_out, Entrada1);
  not not_179 (not_179_out, Entrada8);
  not not_180 (not_180_out, Entrada7);
  not not_181 (not_181_out, Entrada5);
  not not_182 (not_182_out, Entrada4);
  not not_183 (not_183_out, Entrada1);
  not not_184 (not_184_out, Entrada8);
  not not_185 (not_185_out, Entrada6);
  not not_186 (not_186_out, Entrada5);
  not not_187 (not_187_out, Entrada4);
  not not_188 (not_188_out, Entrada2);
  not not_189 (not_189_out, Entrada8);
  not not_190 (not_190_out, Entrada7);
  not not_191 (not_191_out, Entrada6);
  not not_192 (not_192_out, Entrada3);
  not not_193 (not_193_out, Entrada2);
  not not_194 (not_194_out, Entrada8);
  not not_195 (not_195_out, Entrada6);
  not not_196 (not_196_out, Entrada1);
  not not_197 (not_197_out, Entrada8);
  not not_198 (not_198_out, Entrada6);
  not not_199 (not_199_out, Entrada5);
  not not_200 (not_200_out, Entrada8);
  not not_201 (not_201_out, Entrada7);
  not not_202 (not_202_out, Entrada3);
  not not_203 (not_203_out, Entrada1);
  not not_204 (not_204_out, Entrada8);
  not not_205 (not_205_out, Entrada7);
  not not_206 (not_206_out, Entrada6);
  not not_207 (not_207_out, Entrada4);
  not not_208 (not_208_out, Entrada3);
  not not_209 (not_209_out, Entrada7);
  not not_210 (not_210_out, Entrada6);
  not not_211 (not_211_out, Entrada2);
  not not_212 (not_212_out, Entrada1);
  not not_213 (not_213_out, Entrada8);
  not not_214 (not_214_out, Entrada7);
  not not_215 (not_215_out, Entrada6);
  not not_216 (not_216_out, Entrada2);
  not not_217 (not_217_out, Entrada8);
  not not_218 (not_218_out, Entrada6);
  not not_219 (not_219_out, Entrada3);
  not not_220 (not_220_out, Entrada2);
  not not_221 (not_221_out, Entrada8);
  not not_222 (not_222_out, Entrada7);
  not not_223 (not_223_out, Entrada5);
  not not_224 (not_224_out, Entrada4);
  not not_225 (not_225_out, Entrada7);
  not not_226 (not_226_out, Entrada5);
  not not_227 (not_227_out, Entrada1);
  not not_228 (not_228_out, Entrada8);
  not not_229 (not_229_out, Entrada2);
  not not_230 (not_230_out, Entrada1);
  not not_231 (not_231_out, Entrada8);
  not not_232 (not_232_out, Entrada5);
  not not_233 (not_233_out, Entrada2);
  not not_234 (not_234_out, Entrada8);
  not not_235 (not_235_out, Entrada7);
  not not_236 (not_236_out, Entrada4);
  not not_237 (not_237_out, Entrada3);
  not not_238 (not_238_out, Entrada2);
  not not_239 (not_239_out, Entrada8);
  not not_240 (not_240_out, Entrada4);
  not not_241 (not_241_out, Entrada8);
  not not_242 (not_242_out, Entrada7);
  not not_243 (not_243_out, Entrada3);
  not not_244 (not_244_out, Entrada8);
  not not_245 (not_245_out, Entrada6);
  not not_246 (not_246_out, Entrada5);
  not not_247 (not_247_out, Entrada4);
  not not_248 (not_248_out, Entrada2);
  not not_249 (not_249_out, Entrada8);
  not not_250 (not_250_out, Entrada5);
  not not_251 (not_251_out, Entrada4);
  not not_252 (not_252_out, Entrada3);
  not not_253 (not_253_out, Entrada1);
  not not_254 (not_254_out, Entrada8);
  not not_255 (not_255_out, Entrada6);
  not not_256 (not_256_out, Entrada4);
  not not_257 (not_257_out, Entrada2);
  not not_258 (not_258_out, Entrada6);
  not not_259 (not_259_out, Entrada5);
  not not_260 (not_260_out, Entrada1);
  not not_261 (not_261_out, Entrada5);
  not not_262 (not_262_out, Entrada2);
  not not_263 (not_263_out, Entrada1);
  not not_264 (not_264_out, Entrada8);
  not not_265 (not_265_out, Entrada6);
  not not_266 (not_266_out, Entrada5);
  not not_267 (not_267_out, Entrada8);
  not not_268 (not_268_out, Entrada6);
  not not_269 (not_269_out, Entrada8);
  not not_270 (not_270_out, Entrada4);
  not not_271 (not_271_out, Entrada1);
  not not_272 (not_272_out, Entrada8);
  not not_273 (not_273_out, Entrada4);
  not not_274 (not_274_out, Entrada3);
  not not_275 (not_275_out, Entrada8);
  not not_276 (not_276_out, Entrada5);
  not not_277 (not_277_out, Entrada2);
  not not_278 (not_278_out, Entrada8);
  not not_279 (not_279_out, Entrada5);
  not not_280 (not_280_out, Entrada1);
  not not_281 (not_281_out, Entrada8);
  not not_282 (not_282_out, Entrada2);
  not not_283 (not_283_out, Entrada1);
  not not_284 (not_284_out, Entrada7);
  not not_285 (not_285_out, Entrada6);
  not not_286 (not_286_out, Entrada4);
  not not_287 (not_287_out, Entrada3);
  not not_288 (not_288_out, Entrada2);
  not not_289 (not_289_out, Entrada6);
  not not_290 (not_290_out, Entrada4);
  not not_291 (not_291_out, Entrada1);
  not not_292 (not_292_out, Entrada6);
  not not_293 (not_293_out, Entrada5);
  not not_294 (not_294_out, Entrada4);
  not not_295 (not_295_out, Entrada6);
  not not_296 (not_296_out, Entrada5);
  not not_297 (not_297_out, Entrada2);
  not not_298 (not_298_out, Entrada1);
  not not_299 (not_299_out, Entrada7);
  not not_300 (not_300_out, Entrada6);
  not not_301 (not_301_out, Entrada3);
  not not_302 (not_302_out, Entrada7);
  not not_303 (not_303_out, Entrada6);
  not not_304 (not_304_out, Entrada4);
  not not_305 (not_305_out, Entrada2);
  not not_306 (not_306_out, Entrada6);
  not not_307 (not_307_out, Entrada4);
  not not_308 (not_308_out, Entrada3);
  not not_309 (not_309_out, Entrada2);
  not not_310 (not_310_out, Entrada7);
  not not_311 (not_311_out, Entrada6);
  not not_312 (not_312_out, Entrada6);
  not not_313 (not_313_out, Entrada3);
  not not_314 (not_314_out, Entrada4);
  not not_315 (not_315_out, Entrada2);
  not not_316 (not_316_out, Entrada1);
  not not_317 (not_317_out, Entrada5);
  not not_318 (not_318_out, Entrada4);
  not not_319 (not_319_out, Entrada2);
  not not_320 (not_320_out, Entrada7);
  not not_321 (not_321_out, Entrada3);
  not not_322 (not_322_out, Entrada2);
  not not_323 (not_323_out, Entrada1);
  not not_324 (not_324_out, Entrada5);
  not not_325 (not_325_out, Entrada7);
  not not_326 (not_326_out, Entrada4);
  not not_327 (not_327_out, Entrada3);
  not not_328 (not_328_out, Entrada7);
  not not_329 (not_329_out, Entrada2);
  not not_330 (not_330_out, Entrada3);
  not not_331 (not_331_out, Entrada2);
  not not_332 (not_332_out, Entrada6);
  not not_333 (not_333_out, Entrada5);
  not not_334 (not_334_out, Entrada4);
  not not_335 (not_335_out, Entrada6);
  not not_336 (not_336_out, Entrada4);
  not not_337 (not_337_out, Entrada6);
  not not_338 (not_338_out, Entrada2);
  not not_339 (not_339_out, Entrada1);
  not not_340 (not_340_out, Entrada6);
  not not_341 (not_341_out, Entrada5);
  not not_342 (not_342_out, Entrada2);
  not not_343 (not_343_out, Entrada5);
  not not_344 (not_344_out, Entrada4);
  not not_345 (not_345_out, Entrada2);
  not not_346 (not_346_out, Entrada5);
  not not_347 (not_347_out, Entrada4);
  not not_348 (not_348_out, Entrada1);
  not not_349 (not_349_out, Entrada4);
  not not_350 (not_350_out, Entrada2);
  not not_351 (not_351_out, Entrada5);
  not not_352 (not_352_out, Entrada7);
  not not_353 (not_353_out, Entrada6);
  not not_354 (not_354_out, Entrada5);
  not not_355 (not_355_out, Entrada3);
  not not_356 (not_356_out, Entrada1);
  not not_357 (not_357_out, Entrada8);
  not not_358 (not_358_out, Entrada7);
  not not_359 (not_359_out, Entrada6);
  not not_360 (not_360_out, Entrada4);
  not not_361 (not_361_out, Entrada8);
  not not_362 (not_362_out, Entrada7);
  not not_363 (not_363_out, Entrada6);
  not not_364 (not_364_out, Entrada3);
  not not_365 (not_365_out, Entrada1);
  not not_366 (not_366_out, Entrada8);
  not not_367 (not_367_out, Entrada6);
  not not_368 (not_368_out, Entrada4);
  not not_369 (not_369_out, Entrada3);
  not not_370 (not_370_out, Entrada8);
  not not_371 (not_371_out, Entrada6);
  not not_372 (not_372_out, Entrada4);
  not not_373 (not_373_out, Entrada1);
  not not_374 (not_374_out, Entrada7);
  not not_375 (not_375_out, Entrada6);
  not not_376 (not_376_out, Entrada4);
  not not_377 (not_377_out, Entrada3);
  not not_378 (not_378_out, Entrada1);
  not not_379 (not_379_out, Entrada7);
  not not_380 (not_380_out, Entrada5);
  not not_381 (not_381_out, Entrada4);
  not not_382 (not_382_out, Entrada7);
  not not_383 (not_383_out, Entrada5);
  not not_384 (not_384_out, Entrada8);
  not not_385 (not_385_out, Entrada6);
  not not_386 (not_386_out, Entrada5);
  not not_387 (not_387_out, Entrada2);
  not not_388 (not_388_out, Entrada8);
  not not_389 (not_389_out, Entrada6);
  not not_390 (not_390_out, Entrada2);
  not not_391 (not_391_out, Entrada8);
  not not_392 (not_392_out, Entrada5);
  not not_393 (not_393_out, Entrada2);
  not not_394 (not_394_out, Entrada8);
  not not_395 (not_395_out, Entrada7);
  not not_396 (not_396_out, Entrada4);
  not not_397 (not_397_out, Entrada3);
  not not_398 (not_398_out, Entrada1);
  not not_399 (not_399_out, Entrada7);
  not not_400 (not_400_out, Entrada6);
  not not_401 (not_401_out, Entrada3);
  not not_402 (not_402_out, Entrada7);
  not not_403 (not_403_out, Entrada3);
  not not_404 (not_404_out, Entrada2);
  not not_405 (not_405_out, Entrada7);
  not not_406 (not_406_out, Entrada6);
  not not_407 (not_407_out, Entrada1);
  not not_408 (not_408_out, Entrada7);
  not not_409 (not_409_out, Entrada2);
  not not_410 (not_410_out, Entrada1);
  not not_411 (not_411_out, Entrada8);
  not not_412 (not_412_out, Entrada7);
  not not_413 (not_413_out, Entrada4);
  not not_414 (not_414_out, Entrada2);
  not not_415 (not_415_out, Entrada8);
  not not_416 (not_416_out, Entrada7);
  not not_417 (not_417_out, Entrada3);
  not not_418 (not_418_out, Entrada2);
  not not_419 (not_419_out, Entrada1);
  not not_420 (not_420_out, Entrada8);
  not not_421 (not_421_out, Entrada4);
  not not_422 (not_422_out, Entrada3);
  not not_423 (not_423_out, Entrada2);
  not not_424 (not_424_out, Entrada7);
  not not_425 (not_425_out, Entrada4);
  not not_426 (not_426_out, Entrada3);
  not not_427 (not_427_out, Entrada2);
  not not_428 (not_428_out, Entrada1);
  not not_429 (not_429_out, Entrada8);
  not not_430 (not_430_out, Entrada7);
  not not_431 (not_431_out, Entrada5);
  not not_432 (not_432_out, Entrada4);
  not not_433 (not_433_out, Entrada8);
  not not_434 (not_434_out, Entrada7);
  not not_435 (not_435_out, Entrada5);
  not not_436 (not_436_out, Entrada4);
  not not_437 (not_437_out, Entrada8);
  not not_438 (not_438_out, Entrada7);
  not not_439 (not_439_out, Entrada4);
  not not_440 (not_440_out, Entrada8);
  not not_441 (not_441_out, Entrada7);
  not not_442 (not_442_out, Entrada8);
  not not_443 (not_443_out, Entrada3);
  not not_444 (not_444_out, Entrada8);
  not not_445 (not_445_out, Entrada1);
  not not_446 (not_446_out, Entrada8);
  not not_447 (not_447_out, Entrada5);
  not not_448 (not_448_out, Entrada3);
  not not_449 (not_449_out, Entrada5);
  not not_450 (not_450_out, Entrada4);
  not not_451 (not_451_out, Entrada3);
  not not_452 (not_452_out, Entrada8);
  not not_453 (not_453_out, Entrada5);
  not not_454 (not_454_out, Entrada1);
  not not_455 (not_455_out, Entrada6);
  not not_456 (not_456_out, Entrada5);
  not not_457 (not_457_out, Entrada2);
  not not_458 (not_458_out, Entrada8);
  not not_459 (not_459_out, Entrada6);
  not not_460 (not_460_out, Entrada5);
  not not_461 (not_461_out, Entrada6);
  not not_462 (not_462_out, Entrada3);
  not not_463 (not_463_out, Entrada1);
  not not_464 (not_464_out, Entrada3);
  not not_465 (not_465_out, Entrada2);
  not not_466 (not_466_out, Entrada1);
  not not_467 (not_467_out, Entrada8);
  not not_468 (not_468_out, Entrada4);
  not not_469 (not_469_out, Entrada6);
  not not_470 (not_470_out, Entrada3);
  not not_471 (not_471_out, Entrada2);
  not not_472 (not_472_out, Entrada8);
  not not_473 (not_473_out, Entrada4);
  not not_474 (not_474_out, Entrada3);
  not not_475 (not_475_out, Entrada5);
  not not_476 (not_476_out, Entrada3);
  not not_477 (not_477_out, Entrada8);
  not not_478 (not_478_out, Entrada5);
  not not_479 (not_479_out, Entrada4);
  not not_480 (not_480_out, Entrada8);
  not not_481 (not_481_out, Entrada4);
  not not_482 (not_482_out, Entrada1);
  not not_483 (not_483_out, Entrada5);
  not not_484 (not_484_out, Entrada1);
  not not_485 (not_485_out, Entrada7);
  not not_486 (not_486_out, Entrada6);
  not not_487 (not_487_out, Entrada5);
  not not_488 (not_488_out, Entrada2);
  not not_489 (not_489_out, Entrada1);
  not not_490 (not_490_out, Entrada7);
  not not_491 (not_491_out, Entrada5);
  not not_492 (not_492_out, Entrada3);
  not not_493 (not_493_out, Entrada1);
  not not_494 (not_494_out, Entrada6);
  not not_495 (not_495_out, Entrada5);
  not not_496 (not_496_out, Entrada4);
  not not_497 (not_497_out, Entrada2);
  not not_498 (not_498_out, Entrada6);
  not not_499 (not_499_out, Entrada5);
  not not_500 (not_500_out, Entrada3);
  not not_501 (not_501_out, Entrada2);
  not not_502 (not_502_out, Entrada1);
  not not_503 (not_503_out, Entrada7);
  not not_504 (not_504_out, Entrada6);
  not not_505 (not_505_out, Entrada3);
  not not_506 (not_506_out, Entrada2);
  not not_507 (not_507_out, Entrada6);
  not not_508 (not_508_out, Entrada5);
  not not_509 (not_509_out, Entrada6);
  not not_510 (not_510_out, Entrada7);
  not not_511 (not_511_out, Entrada3);
  not not_512 (not_512_out, Entrada7);
  not not_513 (not_513_out, Entrada6);
  not not_514 (not_514_out, Entrada2);
  not not_515 (not_515_out, Entrada7);
  not not_516 (not_516_out, Entrada1);
  not not_517 (not_517_out, Entrada7);
  not not_518 (not_518_out, Entrada4);
  not not_519 (not_519_out, Entrada4);
  not not_520 (not_520_out, Entrada3);
  not not_521 (not_521_out, Entrada5);
  not not_522 (not_522_out, Entrada2);
  not not_523 (not_523_out, Entrada2);
  not not_524 (not_524_out, Entrada4);
  not not_525 (not_525_out, Entrada3);
  not not_526 (not_526_out, Entrada1);
  not not_527 (not_527_out, Entrada6);
  not not_528 (not_528_out, Entrada4);
  not not_529 (not_529_out, Entrada2);
  not not_530 (not_530_out, Entrada6);
  not not_531 (not_531_out, Entrada5);
  not not_532 (not_532_out, Entrada4);
  not not_533 (not_533_out, Entrada5);
  not not_534 (not_534_out, Entrada4);
  not not_535 (not_535_out, Entrada2);
  not not_536 (not_536_out, Entrada6);
  not not_537 (not_537_out, Entrada6);
  not not_538 (not_538_out, Entrada2);
  not not_539 (not_539_out, Entrada1);
  not not_540 (not_540_out, Entrada2);
  not not_541 (not_541_out, Entrada8);
  not not_542 (not_542_out, Entrada7);
  not not_543 (not_543_out, Entrada6);
  not not_544 (not_544_out, Entrada5);
  not not_545 (not_545_out, Entrada3);
  not not_546 (not_546_out, Entrada8);
  not not_547 (not_547_out, Entrada7);
  not not_548 (not_548_out, Entrada6);
  not not_549 (not_549_out, Entrada4);
  not not_550 (not_550_out, Entrada3);
  not not_551 (not_551_out, Entrada8);
  not not_552 (not_552_out, Entrada7);
  not not_553 (not_553_out, Entrada6);
  not not_554 (not_554_out, Entrada3);
  not not_555 (not_555_out, Entrada8);
  not not_556 (not_556_out, Entrada6);
  not not_557 (not_557_out, Entrada4);
  not not_558 (not_558_out, Entrada7);
  not not_559 (not_559_out, Entrada6);
  not not_560 (not_560_out, Entrada4);
  not not_561 (not_561_out, Entrada3);
  not not_562 (not_562_out, Entrada7);
  not not_563 (not_563_out, Entrada6);
  not not_564 (not_564_out, Entrada5);
  not not_565 (not_565_out, Entrada2);
  not not_566 (not_566_out, Entrada1);
  not not_567 (not_567_out, Entrada8);
  not not_568 (not_568_out, Entrada7);
  not not_569 (not_569_out, Entrada6);
  not not_570 (not_570_out, Entrada2);
  not not_571 (not_571_out, Entrada1);
  not not_572 (not_572_out, Entrada8);
  not not_573 (not_573_out, Entrada6);
  not not_574 (not_574_out, Entrada5);
  not not_575 (not_575_out, Entrada2);
  not not_576 (not_576_out, Entrada8);
  not not_577 (not_577_out, Entrada6);
  not not_578 (not_578_out, Entrada5);
  not not_579 (not_579_out, Entrada1);
  not not_580 (not_580_out, Entrada8);
  not not_581 (not_581_out, Entrada7);
  not not_582 (not_582_out, Entrada4);
  not not_583 (not_583_out, Entrada3);
  not not_584 (not_584_out, Entrada8);
  not not_585 (not_585_out, Entrada7);
  not not_586 (not_586_out, Entrada6);
  not not_587 (not_587_out, Entrada8);
  not not_588 (not_588_out, Entrada7);
  not not_589 (not_589_out, Entrada2);
  not not_590 (not_590_out, Entrada8);
  not not_591 (not_591_out, Entrada7);
  not not_592 (not_592_out, Entrada4);
  not not_593 (not_593_out, Entrada3);
  not not_594 (not_594_out, Entrada2);
  not not_595 (not_595_out, Entrada8);
  not not_596 (not_596_out, Entrada7);
  not not_597 (not_597_out, Entrada3);
  not not_598 (not_598_out, Entrada2);
  not not_599 (not_599_out, Entrada8);
  not not_600 (not_600_out, Entrada4);
  not not_601 (not_601_out, Entrada2);
  not not_602 (not_602_out, Entrada7);
  not not_603 (not_603_out, Entrada4);
  not not_604 (not_604_out, Entrada3);
  not not_605 (not_605_out, Entrada2);
  not not_606 (not_606_out, Entrada8);
  not not_607 (not_607_out, Entrada7);
  not not_608 (not_608_out, Entrada3);
  not not_609 (not_609_out, Entrada1);
  not not_610 (not_610_out, Entrada8);
  not not_611 (not_611_out, Entrada4);
  not not_612 (not_612_out, Entrada1);
  not not_613 (not_613_out, Entrada7);
  not not_614 (not_614_out, Entrada4);
  not not_615 (not_615_out, Entrada3);
  not not_616 (not_616_out, Entrada1);
  not not_617 (not_617_out, Entrada8);
  not not_618 (not_618_out, Entrada5);
  not not_619 (not_619_out, Entrada4);
  not not_620 (not_620_out, Entrada8);
  not not_621 (not_621_out, Entrada5);
  not not_622 (not_622_out, Entrada2);
  not not_623 (not_623_out, Entrada1);
  not not_624 (not_624_out, Entrada7);
  not not_625 (not_625_out, Entrada5);
  not not_626 (not_626_out, Entrada3);
  not not_627 (not_627_out, Entrada8);
  not not_628 (not_628_out, Entrada7);
  not not_629 (not_629_out, Entrada6);
  not not_630 (not_630_out, Entrada5);
  not not_631 (not_631_out, Entrada3);
  not not_632 (not_632_out, Entrada2);
  not not_633 (not_633_out, Entrada1);
  not not_634 (not_634_out, Entrada8);
  not not_635 (not_635_out, Entrada5);
  not not_636 (not_636_out, Entrada4);
  not not_637 (not_637_out, Entrada8);
  not not_638 (not_638_out, Entrada5);
  not not_639 (not_639_out, Entrada5);
  not not_640 (not_640_out, Entrada4);
  not not_641 (not_641_out, Entrada5);
  not not_642 (not_642_out, Entrada8);
  not not_643 (not_643_out, Entrada6);
  not not_644 (not_644_out, Entrada3);
  not not_645 (not_645_out, Entrada8);
  not not_646 (not_646_out, Entrada3);
  not not_647 (not_647_out, Entrada2);
  not not_648 (not_648_out, Entrada6);
  not not_649 (not_649_out, Entrada2);
  not not_650 (not_650_out, Entrada1);
  not not_651 (not_651_out, Entrada8);
  not not_652 (not_652_out, Entrada6);
  not not_653 (not_653_out, Entrada2);
  not not_654 (not_654_out, Entrada8);
  not not_655 (not_655_out, Entrada6);
  not not_656 (not_656_out, Entrada1);
  not not_657 (not_657_out, Entrada8);
  not not_658 (not_658_out, Entrada5);
  not not_659 (not_659_out, Entrada4);
  not not_660 (not_660_out, Entrada8);
  not not_661 (not_661_out, Entrada4);
  not not_662 (not_662_out, Entrada5);
  not not_663 (not_663_out, Entrada8);
  not not_664 (not_664_out, Entrada2);
  not not_665 (not_665_out, Entrada1);
  not not_666 (not_666_out, Entrada3);
  not not_667 (not_667_out, Entrada7);
  not not_668 (not_668_out, Entrada5);
  not not_669 (not_669_out, Entrada4);
  not not_670 (not_670_out, Entrada3);
  not not_671 (not_671_out, Entrada6);
  not not_672 (not_672_out, Entrada5);
  not not_673 (not_673_out, Entrada4);
  not not_674 (not_674_out, Entrada1);
  not not_675 (not_675_out, Entrada6);
  not not_676 (not_676_out, Entrada4);
  not not_677 (not_677_out, Entrada2);
  not not_678 (not_678_out, Entrada7);
  not not_679 (not_679_out, Entrada6);
  not not_680 (not_680_out, Entrada2);
  not not_681 (not_681_out, Entrada7);
  not not_682 (not_682_out, Entrada6);
  not not_683 (not_683_out, Entrada5);
  not not_684 (not_684_out, Entrada7);
  not not_685 (not_685_out, Entrada6);
  not not_686 (not_686_out, Entrada1);
  not not_687 (not_687_out, Entrada7);
  not not_688 (not_688_out, Entrada6);
  not not_689 (not_689_out, Entrada3);
  not not_690 (not_690_out, Entrada2);
  not not_691 (not_691_out, Entrada1);
  not not_692 (not_692_out, Entrada7);
  not not_693 (not_693_out, Entrada4);
  not not_694 (not_694_out, Entrada6);
  not not_695 (not_695_out, Entrada5);
  not not_696 (not_696_out, Entrada4);
  not not_697 (not_697_out, Entrada2);
  not not_698 (not_698_out, Entrada1);
  not not_699 (not_699_out, Entrada7);
  not not_700 (not_700_out, Entrada3);
  not not_701 (not_701_out, Entrada4);
  not not_702 (not_702_out, Entrada7);
  not not_703 (not_703_out, Entrada5);
  not not_704 (not_704_out, Entrada1);
  not not_705 (not_705_out, Entrada7);
  not not_706 (not_706_out, Entrada2);
  not not_707 (not_707_out, Entrada1);
  not not_708 (not_708_out, Entrada5);
  not not_709 (not_709_out, Entrada2);
  not not_710 (not_710_out, Entrada6);
  not not_711 (not_711_out, Entrada3);
  not not_712 (not_712_out, Entrada2);
  not not_713 (not_713_out, Entrada6);
  not not_714 (not_714_out, Entrada5);
  not not_715 (not_715_out, Entrada2);
  not not_716 (not_716_out, Entrada1);
  not not_717 (not_717_out, Entrada5);
  not not_718 (not_718_out, Entrada3);
  not not_719 (not_719_out, Entrada1);
  not not_720 (not_720_out, Entrada6);
  not not_721 (not_721_out, Entrada3);
  not not_722 (not_722_out, Entrada6);
  not not_723 (not_723_out, Entrada4);
  not not_724 (not_724_out, Entrada1);
  not not_725 (not_725_out, Entrada4);
  not not_726 (not_726_out, Entrada3);
  not not_727 (not_727_out, Entrada2);
  not not_728 (not_728_out, Entrada4);
  not not_729 (not_729_out, Entrada2);
  not not_730 (not_730_out, Entrada1);
  not not_731 (not_731_out, Entrada1);
  not not_732 (not_732_out, Entrada7);
  not not_733 (not_733_out, Entrada6);
  not not_734 (not_734_out, Entrada5);
  not not_735 (not_735_out, Entrada3);
  not not_736 (not_736_out, Entrada1);
  not not_737 (not_737_out, Entrada8);
  not not_738 (not_738_out, Entrada7);
  not not_739 (not_739_out, Entrada6);
  not not_740 (not_740_out, Entrada3);
  not not_741 (not_741_out, Entrada1);
  not not_742 (not_742_out, Entrada8);
  not not_743 (not_743_out, Entrada6);
  not not_744 (not_744_out, Entrada4);
  not not_745 (not_745_out, Entrada1);
  not not_746 (not_746_out, Entrada7);
  not not_747 (not_747_out, Entrada6);
  not not_748 (not_748_out, Entrada4);
  not not_749 (not_749_out, Entrada3);
  not not_750 (not_750_out, Entrada1);
  not not_751 (not_751_out, Entrada8);
  not not_752 (not_752_out, Entrada6);
  not not_753 (not_753_out, Entrada5);
  not not_754 (not_754_out, Entrada2);
  not not_755 (not_755_out, Entrada1);
  not not_756 (not_756_out, Entrada8);
  not not_757 (not_757_out, Entrada7);
  not not_758 (not_758_out, Entrada4);
  not not_759 (not_759_out, Entrada3);
  not not_760 (not_760_out, Entrada1);
  not not_761 (not_761_out, Entrada7);
  not not_762 (not_762_out, Entrada6);
  not not_763 (not_763_out, Entrada1);
  not not_764 (not_764_out, Entrada7);
  not not_765 (not_765_out, Entrada2);
  not not_766 (not_766_out, Entrada1);
  not not_767 (not_767_out, Entrada8);
  not not_768 (not_768_out, Entrada7);
  not not_769 (not_769_out, Entrada3);
  not not_770 (not_770_out, Entrada2);
  not not_771 (not_771_out, Entrada1);
  not not_772 (not_772_out, Entrada8);
  not not_773 (not_773_out, Entrada4);
  not not_774 (not_774_out, Entrada2);
  not not_775 (not_775_out, Entrada1);
  not not_776 (not_776_out, Entrada7);
  not not_777 (not_777_out, Entrada4);
  not not_778 (not_778_out, Entrada3);
  not not_779 (not_779_out, Entrada2);
  not not_780 (not_780_out, Entrada1);
  not not_781 (not_781_out, Entrada8);
  not not_782 (not_782_out, Entrada5);
  not not_783 (not_783_out, Entrada4);
  not not_784 (not_784_out, Entrada1);
  not not_785 (not_785_out, Entrada8);
  not not_786 (not_786_out, Entrada1);
  not not_787 (not_787_out, Entrada8);
  not not_788 (not_788_out, Entrada5);
  not not_789 (not_789_out, Entrada1);
  not not_790 (not_790_out, Entrada5);
  not not_791 (not_791_out, Entrada4);
  not not_792 (not_792_out, Entrada1);
  not not_793 (not_793_out, Entrada8);
  not not_794 (not_794_out, Entrada6);
  not not_795 (not_795_out, Entrada2);
  not not_796 (not_796_out, Entrada1);
  not not_797 (not_797_out, Entrada6);
  not not_798 (not_798_out, Entrada3);
  not not_799 (not_799_out, Entrada1);
  not not_800 (not_800_out, Entrada3);
  not not_801 (not_801_out, Entrada2);
  not not_802 (not_802_out, Entrada1);
  not not_803 (not_803_out, Entrada8);
  not not_804 (not_804_out, Entrada5);
  not not_805 (not_805_out, Entrada4);
  not not_806 (not_806_out, Entrada1);
  not not_807 (not_807_out, Entrada8);
  not not_808 (not_808_out, Entrada4);
  not not_809 (not_809_out, Entrada1);
  not not_810 (not_810_out, Entrada5);
  not not_811 (not_811_out, Entrada1);
  not not_812 (not_812_out, Entrada7);
  not not_813 (not_813_out, Entrada6);
  not not_814 (not_814_out, Entrada5);
  not not_815 (not_815_out, Entrada2);
  not not_816 (not_816_out, Entrada1);
  not not_817 (not_817_out, Entrada7);
  not not_818 (not_818_out, Entrada5);
  not not_819 (not_819_out, Entrada3);
  not not_820 (not_820_out, Entrada1);
  not not_821 (not_821_out, Entrada6);
  not not_822 (not_822_out, Entrada5);
  not not_823 (not_823_out, Entrada3);
  not not_824 (not_824_out, Entrada2);
  not not_825 (not_825_out, Entrada1);
  not not_826 (not_826_out, Entrada7);
  not not_827 (not_827_out, Entrada6);
  not not_828 (not_828_out, Entrada2);
  not not_829 (not_829_out, Entrada1);
  not not_830 (not_830_out, Entrada6);
  not not_831 (not_831_out, Entrada5);
  not not_832 (not_832_out, Entrada1);
  not not_833 (not_833_out, Entrada7);
  not not_834 (not_834_out, Entrada1);
  not not_835 (not_835_out, Entrada7);
  not not_836 (not_836_out, Entrada3);
  not not_837 (not_837_out, Entrada1);
  not not_838 (not_838_out, Entrada4);
  not not_839 (not_839_out, Entrada1);
  not not_840 (not_840_out, Entrada5);
  not not_841 (not_841_out, Entrada2);
  not not_842 (not_842_out, Entrada1);
  not not_843 (not_843_out, Entrada6);
  not not_844 (not_844_out, Entrada2);
  not not_845 (not_845_out, Entrada1);
  not not_846 (not_846_out, Entrada3);
  not not_847 (not_847_out, Entrada1);
  not not_848 (not_848_out, Entrada6);
  not not_849 (not_849_out, Entrada1);
  not not_850 (not_850_out, Entrada2);
  not not_851 (not_851_out, Entrada1);
  not not_852 (not_852_out, Entrada7);
  not not_853 (not_853_out, Entrada6);
  not not_854 (not_854_out, Entrada5);
  not not_855 (not_855_out, Entrada3);
  not not_856 (not_856_out, Entrada1);
  not not_857 (not_857_out, Entrada8);
  not not_858 (not_858_out, Entrada7);
  not not_859 (not_859_out, Entrada6);
  not not_860 (not_860_out, Entrada4);
  not not_861 (not_861_out, Entrada3);
  not not_862 (not_862_out, Entrada8);
  not not_863 (not_863_out, Entrada7);
  not not_864 (not_864_out, Entrada6);
  not not_865 (not_865_out, Entrada3);
  not not_866 (not_866_out, Entrada1);
  not not_867 (not_867_out, Entrada8);
  not not_868 (not_868_out, Entrada6);
  not not_869 (not_869_out, Entrada4);
  not not_870 (not_870_out, Entrada1);
  not not_871 (not_871_out, Entrada7);
  not not_872 (not_872_out, Entrada6);
  not not_873 (not_873_out, Entrada4);
  not not_874 (not_874_out, Entrada3);
  not not_875 (not_875_out, Entrada1);
  not not_876 (not_876_out, Entrada8);
  not not_877 (not_877_out, Entrada7);
  not not_878 (not_878_out, Entrada6);
  not not_879 (not_879_out, Entrada5);
  not not_880 (not_880_out, Entrada2);
  not not_881 (not_881_out, Entrada8);
  not not_882 (not_882_out, Entrada7);
  not not_883 (not_883_out, Entrada6);
  not not_884 (not_884_out, Entrada5);
  not not_885 (not_885_out, Entrada2);
  not not_886 (not_886_out, Entrada8);
  not not_887 (not_887_out, Entrada7);
  not not_888 (not_888_out, Entrada6);
  not not_889 (not_889_out, Entrada5);
  not not_890 (not_890_out, Entrada8);
  not not_891 (not_891_out, Entrada7);
  not not_892 (not_892_out, Entrada5);
  not not_893 (not_893_out, Entrada2);
  not not_894 (not_894_out, Entrada8);
  not not_895 (not_895_out, Entrada7);
  not not_896 (not_896_out, Entrada4);
  not not_897 (not_897_out, Entrada3);
  not not_898 (not_898_out, Entrada1);
  not not_899 (not_899_out, Entrada8);
  not not_900 (not_900_out, Entrada7);
  not not_901 (not_901_out, Entrada6);
  not not_902 (not_902_out, Entrada4);
  not not_903 (not_903_out, Entrada8);
  not not_904 (not_904_out, Entrada6);
  not not_905 (not_905_out, Entrada4);
  not not_906 (not_906_out, Entrada3);
  not not_907 (not_907_out, Entrada7);
  not not_908 (not_908_out, Entrada6);
  not not_909 (not_909_out, Entrada1);
  not not_910 (not_910_out, Entrada7);
  not not_911 (not_911_out, Entrada2);
  not not_912 (not_912_out, Entrada1);
  not not_913 (not_913_out, Entrada7);
  not not_914 (not_914_out, Entrada6);
  not not_915 (not_915_out, Entrada3);
  not not_916 (not_916_out, Entrada2);
  not not_917 (not_917_out, Entrada8);
  not not_918 (not_918_out, Entrada6);
  not not_919 (not_919_out, Entrada2);
  not not_920 (not_920_out, Entrada8);
  not not_921 (not_921_out, Entrada7);
  not not_922 (not_922_out, Entrada4);
  not not_923 (not_923_out, Entrada3);
  not not_924 (not_924_out, Entrada2);
  not not_925 (not_925_out, Entrada8);
  not not_926 (not_926_out, Entrada7);
  not not_927 (not_927_out, Entrada3);
  not not_928 (not_928_out, Entrada2);
  not not_929 (not_929_out, Entrada1);
  not not_930 (not_930_out, Entrada8);
  not not_931 (not_931_out, Entrada4);
  not not_932 (not_932_out, Entrada2);
  not not_933 (not_933_out, Entrada1);
  not not_934 (not_934_out, Entrada7);
  not not_935 (not_935_out, Entrada4);
  not not_936 (not_936_out, Entrada3);
  not not_937 (not_937_out, Entrada2);
  not not_938 (not_938_out, Entrada1);
  not not_939 (not_939_out, Entrada8);
  not not_940 (not_940_out, Entrada5);
  not not_941 (not_941_out, Entrada4);
  not not_942 (not_942_out, Entrada8);
  not not_943 (not_943_out, Entrada5);
  not not_944 (not_944_out, Entrada4);
  not not_945 (not_945_out, Entrada1);
  not not_946 (not_946_out, Entrada8);
  not not_947 (not_947_out, Entrada7);
  not not_948 (not_948_out, Entrada3);
  not not_949 (not_949_out, Entrada8);
  not not_950 (not_950_out, Entrada1);
  not not_951 (not_951_out, Entrada8);
  not not_952 (not_952_out, Entrada7);
  not not_953 (not_953_out, Entrada4);
  not not_954 (not_954_out, Entrada8);
  not not_955 (not_955_out, Entrada7);
  not not_956 (not_956_out, Entrada8);
  not not_957 (not_957_out, Entrada3);
  not not_958 (not_958_out, Entrada8);
  not not_959 (not_959_out, Entrada6);
  not not_960 (not_960_out, Entrada5);
  not not_961 (not_961_out, Entrada4);
  not not_962 (not_962_out, Entrada2);
  not not_963 (not_963_out, Entrada8);
  not not_964 (not_964_out, Entrada5);
  not not_965 (not_965_out, Entrada1);
  not not_966 (not_966_out, Entrada5);
  not not_967 (not_967_out, Entrada4);
  not not_968 (not_968_out, Entrada1);
  not not_969 (not_969_out, Entrada8);
  not not_970 (not_970_out, Entrada6);
  not not_971 (not_971_out, Entrada4);
  not not_972 (not_972_out, Entrada2);
  not not_973 (not_973_out, Entrada8);
  not not_974 (not_974_out, Entrada6);
  not not_975 (not_975_out, Entrada3);
  not not_976 (not_976_out, Entrada2);
  not not_977 (not_977_out, Entrada8);
  not not_978 (not_978_out, Entrada6);
  not not_979 (not_979_out, Entrada5);
  not not_980 (not_980_out, Entrada6);
  not not_981 (not_981_out, Entrada3);
  not not_982 (not_982_out, Entrada1);
  not not_983 (not_983_out, Entrada3);
  not not_984 (not_984_out, Entrada2);
  not not_985 (not_985_out, Entrada1);
  not not_986 (not_986_out, Entrada8);
  not not_987 (not_987_out, Entrada6);
  not not_988 (not_988_out, Entrada8);
  not not_989 (not_989_out, Entrada5);
  not not_990 (not_990_out, Entrada4);
  not not_991 (not_991_out, Entrada1);
  not not_992 (not_992_out, Entrada8);
  not not_993 (not_993_out, Entrada4);
  not not_994 (not_994_out, Entrada8);
  not not_995 (not_995_out, Entrada5);
  not not_996 (not_996_out, Entrada2);
  not not_997 (not_997_out, Entrada8);
  not not_998 (not_998_out, Entrada2);
  not not_999 (not_999_out, Entrada8);
  not not_1000 (not_1000_out, Entrada4);
  not not_1001 (not_1001_out, Entrada3);
  not not_1002 (not_1002_out, Entrada7);
  not not_1003 (not_1003_out, Entrada6);
  not not_1004 (not_1004_out, Entrada5);
  not not_1005 (not_1005_out, Entrada2);
  not not_1006 (not_1006_out, Entrada1);
  not not_1007 (not_1007_out, Entrada7);
  not not_1008 (not_1008_out, Entrada5);
  not not_1009 (not_1009_out, Entrada3);
  not not_1010 (not_1010_out, Entrada1);
  not not_1011 (not_1011_out, Entrada7);
  not not_1012 (not_1012_out, Entrada6);
  not not_1013 (not_1013_out, Entrada4);
  not not_1014 (not_1014_out, Entrada2);
  not not_1015 (not_1015_out, Entrada7);
  not not_1016 (not_1016_out, Entrada6);
  not not_1017 (not_1017_out, Entrada5);
  not not_1018 (not_1018_out, Entrada4);
  not not_1019 (not_1019_out, Entrada7);
  not not_1020 (not_1020_out, Entrada5);
  not not_1021 (not_1021_out, Entrada4);
  not not_1022 (not_1022_out, Entrada2);
  not not_1023 (not_1023_out, Entrada6);
  not not_1024 (not_1024_out, Entrada3);
  not not_1025 (not_1025_out, Entrada2);
  not not_1026 (not_1026_out, Entrada1);
  not not_1027 (not_1027_out, Entrada6);
  not not_1028 (not_1028_out, Entrada5);
  not not_1029 (not_1029_out, Entrada3);
  not not_1030 (not_1030_out, Entrada6);
  not not_1031 (not_1031_out, Entrada5);
  not not_1032 (not_1032_out, Entrada1);
  not not_1033 (not_1033_out, Entrada7);
  not not_1034 (not_1034_out, Entrada6);
  not not_1035 (not_1035_out, Entrada7);
  not not_1036 (not_1036_out, Entrada1);
  not not_1037 (not_1037_out, Entrada7);
  not not_1038 (not_1038_out, Entrada4);
  not not_1039 (not_1039_out, Entrada3);
  not not_1040 (not_1040_out, Entrada7);
  not not_1041 (not_1041_out, Entrada3);
  not not_1042 (not_1042_out, Entrada1);
  not not_1043 (not_1043_out, Entrada4);
  not not_1044 (not_1044_out, Entrada1);
  not not_1045 (not_1045_out, Entrada5);
  not not_1046 (not_1046_out, Entrada2);
  not not_1047 (not_1047_out, Entrada1);
  not not_1048 (not_1048_out, Entrada7);
  not not_1049 (not_1049_out, Entrada2);
  not not_1050 (not_1050_out, Entrada7);
  not not_1051 (not_1051_out, Entrada5);
  not not_1052 (not_1052_out, Entrada7);
  not not_1053 (not_1053_out, Entrada4);
  not not_1054 (not_1054_out, Entrada4);
  not not_1055 (not_1055_out, Entrada3);
  not not_1056 (not_1056_out, Entrada6);
  not not_1057 (not_1057_out, Entrada4);
  not not_1058 (not_1058_out, Entrada3);
  not not_1059 (not_1059_out, Entrada2);
  not not_1060 (not_1060_out, Entrada6);
  not not_1061 (not_1061_out, Entrada5);
  not not_1062 (not_1062_out, Entrada4);
  not not_1063 (not_1063_out, Entrada6);
  not not_1064 (not_1064_out, Entrada5);
  not not_1065 (not_1065_out, Entrada2);
  not not_1066 (not_1066_out, Entrada6);
  not not_1067 (not_1067_out, Entrada4);
  not not_1068 (not_1068_out, Entrada2);
  not not_1069 (not_1069_out, Entrada6);
  not not_1070 (not_1070_out, Entrada2);
  not not_1071 (not_1071_out, Entrada1);
  not not_1072 (not_1072_out, Entrada3);
  not not_1073 (not_1073_out, Entrada1);
  not not_1074 (not_1074_out, Entrada6);
  not not_1075 (not_1075_out, Entrada4);
  not not_1076 (not_1076_out, Entrada6);
  not not_1077 (not_1077_out, Entrada5);
  not not_1078 (not_1078_out, Entrada4);
  not not_1079 (not_1079_out, Entrada2);
  not not_1080 (not_1080_out, Entrada4);
  not not_1081 (not_1081_out, Entrada2);
  not not_1082 (not_1082_out, Entrada5);
  not not_1083 (not_1083_out, Entrada3);
  not not_1084 (not_1084_out, Entrada5);
  not not_1085 (not_1085_out, Entrada2);
  not not_1086 (not_1086_out, Entrada8);
  not not_1087 (not_1087_out, Entrada6);
  not not_1088 (not_1088_out, Entrada4);
  not not_1089 (not_1089_out, Entrada2);
  not not_1090 (not_1090_out, Entrada7);
  not not_1091 (not_1091_out, Entrada6);
  not not_1092 (not_1092_out, Entrada5);
  not not_1093 (not_1093_out, Entrada3);
  not not_1094 (not_1094_out, Entrada2);
  not not_1095 (not_1095_out, Entrada8);
  not not_1096 (not_1096_out, Entrada7);
  not not_1097 (not_1097_out, Entrada5);
  not not_1098 (not_1098_out, Entrada4);
  not not_1099 (not_1099_out, Entrada8);
  not not_1100 (not_1100_out, Entrada6);
  not not_1101 (not_1101_out, Entrada8);
  not not_1102 (not_1102_out, Entrada7);
  not not_1103 (not_1103_out, Entrada3);
  not not_1104 (not_1104_out, Entrada7);
  not not_1105 (not_1105_out, Entrada4);
  not not_1106 (not_1106_out, Entrada3);
  not not_1107 (not_1107_out, Entrada7);
  not not_1108 (not_1108_out, Entrada6);
  not not_1109 (not_1109_out, Entrada2);
  not not_1110 (not_1110_out, Entrada8);
  not not_1111 (not_1111_out, Entrada7);
  not not_1112 (not_1112_out, Entrada4);
  not not_1113 (not_1113_out, Entrada8);
  not not_1114 (not_1114_out, Entrada2);
  not not_1115 (not_1115_out, Entrada8);
  not not_1116 (not_1116_out, Entrada5);
  not not_1117 (not_1117_out, Entrada8);
  not not_1118 (not_1118_out, Entrada4);
  not not_1119 (not_1119_out, Entrada8);
  not not_1120 (not_1120_out, Entrada5);
  not not_1121 (not_1121_out, Entrada4);
  not not_1122 (not_1122_out, Entrada3);
  not not_1123 (not_1123_out, Entrada6);
  not not_1124 (not_1124_out, Entrada5);
  not not_1125 (not_1125_out, Entrada5);
  not not_1126 (not_1126_out, Entrada2);
  not not_1127 (not_1127_out, Entrada6);
  not not_1128 (not_1128_out, Entrada3);
  not not_1129 (not_1129_out, Entrada2);
  not not_1130 (not_1130_out, Entrada8);
  not not_1131 (not_1131_out, Entrada4);
  not not_1132 (not_1132_out, Entrada5);
  not not_1133 (not_1133_out, Entrada3);
  not not_1134 (not_1134_out, Entrada7);
  not not_1135 (not_1135_out, Entrada6);
  not not_1136 (not_1136_out, Entrada3);
  not not_1137 (not_1137_out, Entrada6);
  not not_1138 (not_1138_out, Entrada4);
  not not_1139 (not_1139_out, Entrada6);
  not not_1140 (not_1140_out, Entrada5);
  not not_1141 (not_1141_out, Entrada2);
  not not_1142 (not_1142_out, Entrada6);
  not not_1143 (not_1143_out, Entrada2);
  not not_1144 (not_1144_out, Entrada7);
  not not_1145 (not_1145_out, Entrada7);
  not not_1146 (not_1146_out, Entrada3);
  not not_1147 (not_1147_out, Entrada2);
  not not_1148 (not_1148_out, Entrada4);
  not not_1149 (not_1149_out, Entrada2);
  not not_1150 (not_1150_out, Entrada5);
  not not_1151 (not_1151_out, Entrada4);
  not not_1152 (not_1152_out, Entrada3);
  and and_1 (and_1_out, not_1_out, not_2_out, not_3_out, not_4_out, not_5_out, Entrada2);
  and and_2 (and_2_out, not_6_out, not_7_out, not_8_out, not_9_out, Entrada3, not_10_out);
  and and_3 (and_3_out, not_11_out, not_12_out, not_13_out, Entrada3, not_14_out);
  and and_4 (and_4_out, not_15_out, not_16_out, not_17_out, Entrada3, not_18_out);
  and and_5 (and_5_out, not_19_out, not_20_out, not_21_out, Entrada4, not_22_out);
  and and_6 (and_6_out, not_23_out, not_24_out, Entrada4, not_25_out, not_26_out);
  and and_7 (and_7_out, not_27_out, not_28_out, not_29_out, not_30_out, Entrada4, Entrada3);
  and and_8 (and_8_out, not_31_out, not_32_out, not_33_out, Entrada4, Entrada3, not_34_out);
  and and_9 (and_9_out, not_35_out, not_36_out, Entrada5, not_37_out, not_38_out);
  and and_10 (and_10_out, not_39_out, Entrada5, not_40_out, not_41_out, not_42_out);
  and and_11 (and_11_out, not_43_out, not_44_out, not_45_out, Entrada5, not_46_out, Entrada2);
  and and_12 (and_12_out, not_47_out, not_48_out, Entrada5, not_49_out, not_50_out, Entrada2);
  and and_13 (and_13_out, not_51_out, not_52_out, Entrada6, not_53_out, not_54_out, not_55_out);
  and and_14 (and_14_out, not_56_out, Entrada6, not_57_out, not_58_out, Entrada2);
  and and_15 (and_15_out, not_59_out, not_60_out, Entrada6, Entrada4, not_61_out, Entrada2);
  and and_16 (and_16_out, not_62_out, not_63_out, Entrada6, Entrada5, not_64_out, Entrada3);
  and and_17 (and_17_out, not_65_out, not_66_out, Entrada6, Entrada5, Entrada4, Entrada2);
  and and_18 (and_18_out, not_67_out, Entrada7, not_68_out, not_69_out, not_70_out, not_71_out);
  and and_19 (and_19_out, not_72_out, Entrada7, not_73_out, not_74_out, not_75_out);
  and and_20 (and_20_out, Entrada7, not_76_out, not_77_out, Entrada3, not_78_out, not_79_out);
  and and_21 (and_21_out, not_80_out, Entrada7, not_81_out, not_82_out, Entrada4, Entrada2);
  and and_22 (and_22_out, not_83_out, Entrada7, not_84_out, Entrada5, Entrada3, not_85_out);
  and and_23 (and_23_out, not_86_out, Entrada7, Entrada5, Entrada3, not_87_out);
  and and_24 (and_24_out, Entrada7, Entrada5, not_88_out, Entrada3, not_89_out);
  and and_25 (and_25_out, not_90_out, Entrada7, not_91_out, Entrada5, Entrada4, Entrada3);
  and and_26 (and_26_out, Entrada7, Entrada6, not_92_out, not_93_out, not_94_out);
  and and_27 (and_27_out, not_95_out, Entrada7, Entrada6, not_96_out, Entrada2);
  and and_28 (and_28_out, not_97_out, Entrada7, Entrada6, not_98_out, Entrada4, not_99_out);
  and and_29 (and_29_out, not_100_out, Entrada7, Entrada6, Entrada4, Entrada3, not_101_out);
  and and_30 (and_30_out, not_102_out, Entrada7, Entrada6, Entrada5, not_103_out, not_104_out);
  and and_31 (and_31_out, not_105_out, Entrada7, Entrada6, Entrada5, not_106_out, Entrada2);
  and and_32 (and_32_out, Entrada8, not_107_out, not_108_out, not_109_out, not_110_out);
  and and_33 (and_33_out, Entrada8, not_111_out, not_112_out, not_113_out, not_114_out, not_115_out);
  and and_34 (and_34_out, Entrada8, not_116_out, not_117_out, not_118_out, not_119_out);
  and and_35 (and_35_out, Entrada8, not_120_out, not_121_out, not_122_out, not_123_out, Entrada3);
  and and_36 (and_36_out, Entrada8, not_124_out, not_125_out, Entrada4, Entrada2);
  and and_37 (and_37_out, Entrada8, not_126_out, Entrada4, not_127_out, Entrada2);
  and and_38 (and_38_out, Entrada8, not_128_out, not_129_out, Entrada5, not_130_out, not_131_out);
  and and_39 (and_39_out, Entrada8, not_132_out, not_133_out, Entrada5, not_134_out, not_135_out);
  and and_40 (and_40_out, Entrada8, not_136_out, Entrada5, not_137_out, not_138_out);
  and and_41 (and_41_out, Entrada8, not_139_out, Entrada5, not_140_out, not_141_out, not_142_out);
  and and_42 (and_42_out, Entrada8, not_143_out, Entrada6, not_144_out, not_145_out, Entrada2);
  and and_43 (and_43_out, Entrada8, Entrada6, not_146_out, not_147_out, Entrada3, not_148_out);
  and and_44 (and_44_out, Entrada8, not_149_out, Entrada6, Entrada4, not_150_out);
  and and_45 (and_45_out, Entrada8, Entrada6, not_151_out, Entrada4, Entrada3, Entrada2);
  and and_46 (and_46_out, Entrada8, not_152_out, Entrada6, Entrada5, not_153_out, Entrada2);
  and and_47 (and_47_out, Entrada8, Entrada6, Entrada5, not_154_out, not_155_out, Entrada2);
  and and_48 (and_48_out, Entrada8, Entrada6, Entrada5, Entrada4, not_156_out);
  and and_49 (and_49_out, Entrada8, Entrada7, not_157_out, not_158_out, not_159_out, Entrada2);
  and and_50 (and_50_out, Entrada8, Entrada7, not_160_out, not_161_out, Entrada4, Entrada3, not_162_out);
  and and_51 (and_51_out, Entrada8, Entrada7, not_163_out, Entrada4, Entrada3, not_164_out);
  and and_52 (and_52_out, Entrada8, Entrada7, not_165_out, Entrada5, not_166_out, Entrada3);
  and and_53 (and_53_out, Entrada8, Entrada7, Entrada5, Entrada4, Entrada3, Entrada2);
  and and_54 (and_54_out, Entrada8, Entrada7, Entrada6, not_167_out, not_168_out, not_169_out);
  and and_55 (and_55_out, Entrada8, Entrada7, Entrada6, not_170_out, Entrada3, not_171_out);
  and and_56 (and_56_out, Entrada8, Entrada7, Entrada6, not_172_out, Entrada4, not_173_out);
  and and_57 (and_57_out, not_174_out, not_175_out, not_176_out, not_177_out, not_178_out);
  and and_58 (and_58_out, not_179_out, not_180_out, not_181_out, not_182_out, Entrada3, not_183_out);
  and and_59 (and_59_out, not_184_out, not_185_out, not_186_out, not_187_out, Entrada3, not_188_out);
  and and_60 (and_60_out, not_189_out, not_190_out, not_191_out, Entrada4, not_192_out, not_193_out);
  and and_61 (and_61_out, not_194_out, not_195_out, Entrada4, Entrada2, not_196_out);
  and and_62 (and_62_out, not_197_out, not_198_out, not_199_out, Entrada4, Entrada3, Entrada2);
  and and_63 (and_63_out, not_200_out, not_201_out, Entrada5, not_202_out, not_203_out);
  and and_64 (and_64_out, not_204_out, not_205_out, not_206_out, Entrada5, not_207_out, not_208_out, Entrada2);
  and and_65 (and_65_out, not_209_out, not_210_out, Entrada5, Entrada3, not_211_out, not_212_out);
  and and_66 (and_66_out, not_213_out, not_214_out, not_215_out, Entrada5, Entrada4, not_216_out);
  and and_67 (and_67_out, not_217_out, not_218_out, Entrada5, Entrada4, not_219_out, not_220_out);
  and and_68 (and_68_out, not_221_out, not_222_out, Entrada6, not_223_out, not_224_out, Entrada2);
  and and_69 (and_69_out, not_225_out, Entrada6, not_226_out, Entrada3, Entrada2, not_227_out);
  and and_70 (and_70_out, not_228_out, Entrada6, Entrada4, not_229_out, not_230_out);
  and and_71 (and_71_out, not_231_out, Entrada6, not_232_out, Entrada4, Entrada3, not_233_out);
  and and_72 (and_72_out, not_234_out, not_235_out, Entrada6, Entrada5, not_236_out, not_237_out, not_238_out);
  and and_73 (and_73_out, not_239_out, Entrada6, Entrada5, not_240_out, Entrada3, Entrada2);
  and and_74 (and_74_out, not_241_out, not_242_out, Entrada6, Entrada5, Entrada4, not_243_out, Entrada2);
  and and_75 (and_75_out, not_244_out, Entrada7, not_245_out, not_246_out, not_247_out, not_248_out);
  and and_76 (and_76_out, not_249_out, Entrada7, not_250_out, not_251_out, not_252_out, not_253_out);
  and and_77 (and_77_out, not_254_out, Entrada7, not_255_out, not_256_out, Entrada3, not_257_out);
  and and_78 (and_78_out, Entrada7, not_258_out, not_259_out, Entrada3, not_260_out);
  and and_79 (and_79_out, Entrada7, not_261_out, Entrada3, not_262_out, not_263_out);
  and and_80 (and_80_out, not_264_out, Entrada7, not_265_out, not_266_out, Entrada4, Entrada2);
  and and_81 (and_81_out, not_267_out, Entrada7, not_268_out, Entrada4, Entrada3, Entrada2);
  and and_82 (and_82_out, not_269_out, Entrada7, Entrada5, not_270_out, Entrada3, not_271_out);
  and and_83 (and_83_out, not_272_out, Entrada7, Entrada6, not_273_out, not_274_out, Entrada2);
  and and_84 (and_84_out, not_275_out, Entrada7, Entrada6, not_276_out, Entrada4, not_277_out);
  and and_85 (and_85_out, not_278_out, Entrada7, Entrada6, not_279_out, Entrada4, not_280_out);
  and and_86 (and_86_out, not_281_out, Entrada7, Entrada6, Entrada4, Entrada3, not_282_out);
  and and_87 (and_87_out, Entrada7, Entrada6, Entrada5, Entrada3, Entrada2, not_283_out);
  and and_88 (and_88_out, Entrada8, not_284_out, not_285_out, not_286_out, not_287_out, not_288_out);
  and and_89 (and_89_out, Entrada8, not_289_out, not_290_out, Entrada2, not_291_out);
  and and_90 (and_90_out, Entrada8, not_292_out, not_293_out, not_294_out, Entrada3, Entrada2);
  and and_91 (and_91_out, Entrada8, not_295_out, not_296_out, Entrada4, not_297_out, not_298_out);
  and and_92 (and_92_out, Entrada8, not_299_out, not_300_out, Entrada4, not_301_out, Entrada2);
  and and_93 (and_93_out, Entrada8, not_302_out, not_303_out, Entrada5, not_304_out, not_305_out);
  and and_94 (and_94_out, Entrada8, not_306_out, Entrada5, not_307_out, not_308_out, not_309_out);
  and and_95 (and_95_out, Entrada8, not_310_out, not_311_out, Entrada5, Entrada4, Entrada2);
  and and_96 (and_96_out, Entrada8, not_312_out, Entrada5, Entrada4, not_313_out, Entrada2);
  and and_97 (and_97_out, Entrada8, Entrada6, not_314_out, not_315_out, not_316_out);
  and and_98 (and_98_out, Entrada8, Entrada6, not_317_out, not_318_out, Entrada3, not_319_out);
  and and_99 (and_99_out, Entrada8, not_320_out, Entrada6, Entrada4, not_321_out, not_322_out);
  and and_100 (and_100_out, Entrada8, Entrada6, Entrada4, Entrada2, not_323_out);
  and and_101 (and_101_out, Entrada8, Entrada6, not_324_out, Entrada4, Entrada3, Entrada2);
  and and_102 (and_102_out, Entrada8, not_325_out, Entrada6, Entrada5, not_326_out, not_327_out, Entrada2);
  and and_103 (and_103_out, Entrada8, not_328_out, Entrada6, Entrada5, Entrada4, not_329_out);
  and and_104 (and_104_out, Entrada8, Entrada6, Entrada5, Entrada4, not_330_out, not_331_out);
  and and_105 (and_105_out, Entrada8, Entrada7, not_332_out, not_333_out, not_334_out, Entrada2);
  and and_106 (and_106_out, Entrada8, Entrada7, not_335_out, not_336_out, Entrada3, Entrada2);
  and and_107 (and_107_out, Entrada8, Entrada7, not_337_out, Entrada4, not_338_out, not_339_out);
  and and_108 (and_108_out, Entrada8, Entrada7, not_340_out, not_341_out, Entrada4, Entrada3, not_342_out);
  and and_109 (and_109_out, Entrada8, Entrada7, Entrada6, not_343_out, not_344_out, not_345_out);
  and and_110 (and_110_out, Entrada8, Entrada7, Entrada6, not_346_out, not_347_out, not_348_out);
  and and_111 (and_111_out, Entrada8, Entrada7, Entrada6, not_349_out, Entrada3, not_350_out);
  and and_112 (and_112_out, Entrada8, Entrada7, Entrada6, not_351_out, Entrada4, Entrada2);
  and and_113 (and_113_out, Entrada8, Entrada7, Entrada6, Entrada4, Entrada3, Entrada2);
  and and_114 (and_114_out, not_352_out, not_353_out, not_354_out, not_355_out, not_356_out);
  and and_115 (and_115_out, not_357_out, not_358_out, not_359_out, not_360_out, Entrada2);
  and and_116 (and_116_out, not_361_out, not_362_out, not_363_out, not_364_out, Entrada2, not_365_out);
  and and_117 (and_117_out, not_366_out, not_367_out, not_368_out, not_369_out, Entrada2);
  and and_118 (and_118_out, not_370_out, not_371_out, not_372_out, Entrada2, not_373_out);
  and and_119 (and_119_out, not_374_out, not_375_out, not_376_out, not_377_out, Entrada2, not_378_out);
  and and_120 (and_120_out, not_379_out, not_380_out, not_381_out, Entrada3, Entrada1);
  and and_121 (and_121_out, not_382_out, not_383_out, Entrada3, Entrada2, Entrada1);
  and and_122 (and_122_out, not_384_out, not_385_out, not_386_out, Entrada4, not_387_out);
  and and_123 (and_123_out, not_388_out, not_389_out, Entrada4, Entrada3, not_390_out);
  and and_124 (and_124_out, not_391_out, not_392_out, Entrada4, Entrada3, not_393_out, Entrada1);
  and and_125 (and_125_out, not_394_out, not_395_out, Entrada5, not_396_out, not_397_out, not_398_out);
  and and_126 (and_126_out, not_399_out, not_400_out, Entrada5, not_401_out, Entrada1);
  and and_127 (and_127_out, not_402_out, Entrada5, not_403_out, not_404_out, Entrada1);
  and and_128 (and_128_out, not_405_out, not_406_out, Entrada5, Entrada3, not_407_out);
  and and_129 (and_129_out, not_408_out, Entrada5, Entrada3, not_409_out, not_410_out);
  and and_130 (and_130_out, not_411_out, not_412_out, Entrada6, not_413_out, not_414_out);
  and and_131 (and_131_out, not_415_out, not_416_out, Entrada6, not_417_out, not_418_out, not_419_out);
  and and_132 (and_132_out, not_420_out, Entrada6, not_421_out, not_422_out, not_423_out);
  and and_133 (and_133_out, not_424_out, Entrada6, not_425_out, not_426_out, not_427_out, not_428_out);
  and and_134 (and_134_out, not_429_out, not_430_out, Entrada6, not_431_out, not_432_out, Entrada1);
  and and_135 (and_135_out, not_433_out, not_434_out, Entrada6, not_435_out, not_436_out, Entrada3);
  and and_136 (and_136_out, not_437_out, not_438_out, Entrada6, not_439_out, Entrada3, Entrada1);
  and and_137 (and_137_out, not_440_out, not_441_out, Entrada6, Entrada4, Entrada2);
  and and_138 (and_138_out, not_442_out, Entrada6, Entrada4, not_443_out, Entrada2);
  and and_139 (and_139_out, not_444_out, Entrada6, Entrada4, Entrada2, not_445_out);
  and and_140 (and_140_out, not_446_out, Entrada7, not_447_out, not_448_out, Entrada1);
  and and_141 (and_141_out, Entrada7, not_449_out, not_450_out, not_451_out, Entrada1);
  and and_142 (and_142_out, not_452_out, Entrada7, not_453_out, Entrada3, not_454_out);
  and and_143 (and_143_out, Entrada7, not_455_out, not_456_out, Entrada3, not_457_out, Entrada1);
  and and_144 (and_144_out, not_458_out, Entrada7, not_459_out, not_460_out, Entrada4, Entrada3);
  and and_145 (and_145_out, Entrada7, not_461_out, Entrada5, not_462_out, not_463_out);
  and and_146 (and_146_out, Entrada7, Entrada5, not_464_out, not_465_out, not_466_out);
  and and_147 (and_147_out, not_467_out, Entrada7, Entrada5, Entrada3, Entrada1);
  and and_148 (and_148_out, Entrada7, Entrada5, not_468_out, Entrada3, Entrada1);
  and and_149 (and_149_out, Entrada7, not_469_out, Entrada5, Entrada4, not_470_out, not_471_out);
  and and_150 (and_150_out, not_472_out, Entrada7, Entrada6, not_473_out, not_474_out, Entrada1);
  and and_151 (and_151_out, Entrada7, Entrada6, not_475_out, not_476_out, Entrada1);
  and and_152 (and_152_out, not_477_out, Entrada7, Entrada6, not_478_out, not_479_out, Entrada2);
  and and_153 (and_153_out, not_480_out, Entrada7, Entrada6, not_481_out, Entrada3, not_482_out);
  and and_154 (and_154_out, Entrada7, Entrada6, not_483_out, Entrada3, not_484_out);
  and and_155 (and_155_out, Entrada8, not_485_out, not_486_out, not_487_out, not_488_out, not_489_out);
  and and_156 (and_156_out, Entrada8, not_490_out, not_491_out, not_492_out, not_493_out);
  and and_157 (and_157_out, Entrada8, not_494_out, not_495_out, not_496_out, not_497_out);
  and and_158 (and_158_out, Entrada8, not_498_out, not_499_out, not_500_out, not_501_out, not_502_out);
  and and_159 (and_159_out, Entrada8, not_503_out, not_504_out, Entrada4, not_505_out, not_506_out);
  and and_160 (and_160_out, Entrada8, not_507_out, not_508_out, Entrada4, Entrada2);
  and and_161 (and_161_out, Entrada8, not_509_out, Entrada4, Entrada3, Entrada2);
  and and_162 (and_162_out, Entrada8, not_510_out, Entrada5, not_511_out, Entrada1);
  and and_163 (and_163_out, Entrada8, not_512_out, not_513_out, Entrada5, Entrada3, not_514_out);
  and and_164 (and_164_out, Entrada8, not_515_out, Entrada5, Entrada3, not_516_out);
  and and_165 (and_165_out, Entrada8, not_517_out, Entrada6, not_518_out, Entrada2);
  and and_166 (and_166_out, Entrada8, Entrada6, not_519_out, not_520_out, Entrada2);
  and and_167 (and_167_out, Entrada8, Entrada6, not_521_out, Entrada4, not_522_out);
  and and_168 (and_168_out, Entrada8, Entrada6, Entrada4, Entrada3, not_523_out);
  and and_169 (and_169_out, Entrada8, Entrada6, Entrada5, not_524_out, Entrada2);
  and and_170 (and_170_out, Entrada8, Entrada6, Entrada5, not_525_out, Entrada2, not_526_out);
  and and_171 (and_171_out, Entrada8, Entrada7, not_527_out, not_528_out, not_529_out);
  and and_172 (and_172_out, Entrada8, Entrada7, not_530_out, not_531_out, not_532_out, Entrada3);
  and and_173 (and_173_out, Entrada8, Entrada7, not_533_out, not_534_out, Entrada3, not_535_out);
  and and_174 (and_174_out, Entrada8, Entrada7, not_536_out, Entrada4, Entrada2);
  and and_175 (and_175_out, Entrada8, Entrada7, not_537_out, Entrada5, not_538_out, not_539_out);
  and and_176 (and_176_out, Entrada8, Entrada7, Entrada6, Entrada4, not_540_out);
  and and_177 (and_177_out, Entrada8, Entrada7, Entrada6, Entrada4, Entrada3, Entrada1);
  and and_178 (and_178_out, not_541_out, not_542_out, not_543_out, not_544_out, not_545_out);
  and and_179 (and_179_out, not_546_out, not_547_out, not_548_out, not_549_out, not_550_out, Entrada1);
  and and_180 (and_180_out, not_551_out, not_552_out, not_553_out, not_554_out, Entrada2, Entrada1);
  and and_181 (and_181_out, not_555_out, not_556_out, not_557_out, Entrada2, Entrada1);
  and and_182 (and_182_out, not_558_out, not_559_out, not_560_out, not_561_out, Entrada2, Entrada1);
  and and_183 (and_183_out, not_562_out, not_563_out, not_564_out, Entrada3, not_565_out, not_566_out);
  and and_184 (and_184_out, not_567_out, not_568_out, not_569_out, Entrada4, not_570_out, not_571_out);
  and and_185 (and_185_out, not_572_out, not_573_out, not_574_out, Entrada4, not_575_out, Entrada1);
  and and_186 (and_186_out, not_576_out, not_577_out, not_578_out, Entrada4, Entrada2, not_579_out);
  and and_187 (and_187_out, not_580_out, not_581_out, Entrada5, not_582_out, not_583_out, Entrada2);
  and and_188 (and_188_out, not_584_out, not_585_out, not_586_out, Entrada5, Entrada3);
  and and_189 (and_189_out, not_587_out, not_588_out, Entrada5, Entrada3, not_589_out);
  and and_190 (and_190_out, not_590_out, not_591_out, Entrada6, not_592_out, not_593_out, not_594_out);
  and and_191 (and_191_out, not_595_out, not_596_out, Entrada6, not_597_out, not_598_out, Entrada1);
  and and_192 (and_192_out, not_599_out, Entrada6, not_600_out, not_601_out, Entrada1);
  and and_193 (and_193_out, not_602_out, Entrada6, not_603_out, not_604_out, not_605_out, Entrada1);
  and and_194 (and_194_out, not_606_out, not_607_out, Entrada6, not_608_out, Entrada2, not_609_out);
  and and_195 (and_195_out, not_610_out, Entrada6, not_611_out, Entrada2, not_612_out);
  and and_196 (and_196_out, not_613_out, Entrada6, not_614_out, not_615_out, Entrada2, not_616_out);
  and and_197 (and_197_out, not_617_out, Entrada6, not_618_out, not_619_out, Entrada3, Entrada2);
  and and_198 (and_198_out, not_620_out, Entrada6, not_621_out, Entrada4, not_622_out, not_623_out);
  and and_199 (and_199_out, not_624_out, Entrada6, not_625_out, Entrada4, not_626_out);
  and and_200 (and_200_out, not_627_out, Entrada6, Entrada4, Entrada2, Entrada1);
  and and_201 (and_201_out, not_628_out, Entrada6, Entrada5, Entrada4, Entrada3);
  and and_202 (and_202_out, Entrada7, not_629_out, not_630_out, not_631_out, not_632_out, not_633_out);
  and and_203 (and_203_out, not_634_out, Entrada7, not_635_out, not_636_out, Entrada3);
  and and_204 (and_204_out, not_637_out, Entrada7, not_638_out, Entrada3, Entrada1);
  and and_205 (and_205_out, Entrada7, not_639_out, not_640_out, Entrada3, Entrada1);
  and and_206 (and_206_out, Entrada7, not_641_out, Entrada3, Entrada2, Entrada1);
  and and_207 (and_207_out, not_642_out, Entrada7, not_643_out, Entrada5, not_644_out);
  and and_208 (and_208_out, not_645_out, Entrada7, Entrada5, not_646_out, not_647_out);
  and and_209 (and_209_out, Entrada7, not_648_out, Entrada5, Entrada3, not_649_out, not_650_out);
  and and_210 (and_210_out, not_651_out, Entrada7, not_652_out, Entrada5, Entrada4, not_653_out);
  and and_211 (and_211_out, not_654_out, Entrada7, not_655_out, Entrada5, Entrada4, not_656_out);
  and and_212 (and_212_out, not_657_out, Entrada7, Entrada6, not_658_out, not_659_out, Entrada2);
  and and_213 (and_213_out, not_660_out, Entrada7, Entrada6, not_661_out, Entrada3, Entrada2);
  and and_214 (and_214_out, Entrada7, Entrada6, not_662_out, Entrada3, Entrada2);
  and and_215 (and_215_out, not_663_out, Entrada7, Entrada6, Entrada4, not_664_out, not_665_out);
  and and_216 (and_216_out, Entrada7, Entrada6, Entrada5, Entrada4, not_666_out);
  and and_217 (and_217_out, Entrada8, not_667_out, not_668_out, not_669_out, not_670_out);
  and and_218 (and_218_out, Entrada8, not_671_out, not_672_out, not_673_out, Entrada2, not_674_out);
  and and_219 (and_219_out, Entrada8, not_675_out, not_676_out, Entrada3, not_677_out, Entrada1);
  and and_220 (and_220_out, Entrada8, not_678_out, not_679_out, Entrada4, not_680_out, Entrada1);
  and and_221 (and_221_out, Entrada8, not_681_out, not_682_out, not_683_out, Entrada4, Entrada2);
  and and_222 (and_222_out, Entrada8, not_684_out, not_685_out, Entrada4, Entrada2, not_686_out);
  and and_223 (and_223_out, Entrada8, not_687_out, not_688_out, Entrada5, not_689_out, not_690_out, not_691_out);
  and and_224 (and_224_out, Entrada8, not_692_out, Entrada5, not_693_out, Entrada3);
  and and_225 (and_225_out, Entrada8, not_694_out, Entrada5, Entrada4, Entrada3, Entrada2);
  and and_226 (and_226_out, Entrada8, Entrada6, not_695_out, not_696_out, not_697_out, not_698_out);
  and and_227 (and_227_out, Entrada8, not_699_out, Entrada6, not_700_out, Entrada2, Entrada1);
  and and_228 (and_228_out, Entrada8, Entrada6, not_701_out, Entrada2, Entrada1);
  and and_229 (and_229_out, Entrada8, not_702_out, Entrada6, not_703_out, Entrada4, not_704_out);
  and and_230 (and_230_out, Entrada8, not_705_out, Entrada6, Entrada4, not_706_out, not_707_out);
  and and_231 (and_231_out, Entrada8, Entrada6, not_708_out, Entrada4, not_709_out, Entrada1);
  and and_232 (and_232_out, Entrada8, Entrada7, not_710_out, not_711_out, not_712_out, Entrada1);
  and and_233 (and_233_out, Entrada8, Entrada7, not_713_out, not_714_out, Entrada4, not_715_out, not_716_out);
  and and_234 (and_234_out, Entrada8, Entrada7, not_717_out, Entrada4, not_718_out, not_719_out);
  and and_235 (and_235_out, Entrada8, Entrada7, not_720_out, Entrada4, not_721_out, Entrada2);
  and and_236 (and_236_out, Entrada8, Entrada7, not_722_out, Entrada5, not_723_out, not_724_out);
  and and_237 (and_237_out, Entrada8, Entrada7, Entrada5, not_725_out, not_726_out);
  and and_238 (and_238_out, Entrada8, Entrada7, Entrada5, Entrada4, Entrada3, not_727_out);
  and and_239 (and_239_out, Entrada8, Entrada7, Entrada6, not_728_out, not_729_out, not_730_out);
  and and_240 (and_240_out, Entrada8, Entrada7, Entrada6, Entrada5, Entrada4, not_731_out);
  and and_241 (and_241_out, not_732_out, not_733_out, not_734_out, not_735_out, not_736_out);
  and and_242 (and_242_out, not_737_out, not_738_out, not_739_out, not_740_out, Entrada2, not_741_out);
  and and_243 (and_243_out, not_742_out, not_743_out, not_744_out, Entrada2, not_745_out);
  and and_244 (and_244_out, not_746_out, not_747_out, not_748_out, not_749_out, Entrada2, not_750_out);
  and and_245 (and_245_out, not_751_out, not_752_out, not_753_out, Entrada4, not_754_out, not_755_out);
  and and_246 (and_246_out, not_756_out, not_757_out, Entrada5, not_758_out, not_759_out, not_760_out);
  and and_247 (and_247_out, not_761_out, not_762_out, Entrada5, Entrada3, not_763_out);
  and and_248 (and_248_out, not_764_out, Entrada5, Entrada3, not_765_out, not_766_out);
  and and_249 (and_249_out, not_767_out, not_768_out, Entrada6, not_769_out, not_770_out, not_771_out);
  and and_250 (and_250_out, not_772_out, Entrada6, not_773_out, not_774_out, not_775_out);
  and and_251 (and_251_out, not_776_out, Entrada6, not_777_out, not_778_out, not_779_out, not_780_out);
  and and_252 (and_252_out, not_781_out, Entrada6, not_782_out, not_783_out, Entrada3, not_784_out);
  and and_253 (and_253_out, not_785_out, Entrada6, Entrada4, Entrada2, not_786_out);
  and and_254 (and_254_out, not_787_out, Entrada7, not_788_out, Entrada3, not_789_out);
  and and_255 (and_255_out, Entrada7, not_790_out, not_791_out, Entrada3, not_792_out);
  and and_256 (and_256_out, not_793_out, Entrada7, not_794_out, Entrada4, not_795_out, not_796_out);
  and and_257 (and_257_out, Entrada7, not_797_out, Entrada5, not_798_out, not_799_out);
  and and_258 (and_258_out, Entrada7, Entrada5, not_800_out, not_801_out, not_802_out);
  and and_259 (and_259_out, not_803_out, Entrada7, Entrada6, not_804_out, not_805_out, not_806_out);
  and and_260 (and_260_out, not_807_out, Entrada7, Entrada6, not_808_out, Entrada3, not_809_out);
  and and_261 (and_261_out, Entrada7, Entrada6, not_810_out, Entrada3, not_811_out);
  and and_262 (and_262_out, Entrada8, not_812_out, not_813_out, not_814_out, not_815_out, not_816_out);
  and and_263 (and_263_out, Entrada8, not_817_out, not_818_out, not_819_out, not_820_out);
  and and_264 (and_264_out, Entrada8, not_821_out, not_822_out, not_823_out, not_824_out, not_825_out);
  and and_265 (and_265_out, Entrada8, not_826_out, not_827_out, Entrada4, not_828_out, not_829_out);
  and and_266 (and_266_out, Entrada8, not_830_out, not_831_out, Entrada4, Entrada2, not_832_out);
  and and_267 (and_267_out, Entrada8, not_833_out, Entrada5, Entrada3, not_834_out);
  and and_268 (and_268_out, Entrada8, not_835_out, Entrada6, not_836_out, Entrada2, not_837_out);
  and and_269 (and_269_out, Entrada8, Entrada6, not_838_out, Entrada2, not_839_out);
  and and_270 (and_270_out, Entrada8, Entrada6, not_840_out, Entrada4, not_841_out, not_842_out);
  and and_271 (and_271_out, Entrada8, Entrada7, not_843_out, Entrada5, not_844_out, not_845_out);
  and and_272 (and_272_out, Entrada8, Entrada7, Entrada5, not_846_out, not_847_out);
  and and_273 (and_273_out, Entrada8, Entrada7, not_848_out, Entrada5, Entrada4, not_849_out);
  and and_274 (and_274_out, Entrada8, Entrada7, Entrada6, Entrada4, not_850_out, not_851_out);
  and and_275 (and_275_out, not_852_out, not_853_out, not_854_out, not_855_out, not_856_out);
  and and_276 (and_276_out, not_857_out, not_858_out, not_859_out, not_860_out, not_861_out, Entrada2);
  and and_277 (and_277_out, not_862_out, not_863_out, not_864_out, not_865_out, Entrada2, not_866_out);
  and and_278 (and_278_out, not_867_out, not_868_out, not_869_out, Entrada2, not_870_out);
  and and_279 (and_279_out, not_871_out, not_872_out, not_873_out, not_874_out, Entrada2, not_875_out);
  and and_280 (and_280_out, not_876_out, not_877_out, not_878_out, not_879_out, Entrada3, not_880_out, Entrada1);
  and and_281 (and_281_out, not_881_out, not_882_out, not_883_out, not_884_out, Entrada4, not_885_out);
  and and_282 (and_282_out, not_886_out, not_887_out, not_888_out, not_889_out, Entrada4, Entrada3, Entrada1);
  and and_283 (and_283_out, not_890_out, not_891_out, not_892_out, Entrada4, Entrada3, not_893_out, Entrada1);
  and and_284 (and_284_out, not_894_out, not_895_out, Entrada5, not_896_out, not_897_out, not_898_out);
  and and_285 (and_285_out, not_899_out, not_900_out, not_901_out, Entrada5, not_902_out, Entrada2);
  and and_286 (and_286_out, not_903_out, not_904_out, Entrada5, not_905_out, not_906_out, Entrada2);
  and and_287 (and_287_out, not_907_out, not_908_out, Entrada5, Entrada3, not_909_out);
  and and_288 (and_288_out, not_910_out, Entrada5, Entrada3, not_911_out, not_912_out);
  and and_289 (and_289_out, not_913_out, not_914_out, Entrada5, Entrada4, not_915_out, not_916_out, Entrada1);
  and and_290 (and_290_out, not_917_out, not_918_out, Entrada5, Entrada4, Entrada3, not_919_out);
  and and_291 (and_291_out, not_920_out, not_921_out, Entrada6, not_922_out, not_923_out, not_924_out);
  and and_292 (and_292_out, not_925_out, not_926_out, Entrada6, not_927_out, not_928_out, not_929_out);
  and and_293 (and_293_out, not_930_out, Entrada6, not_931_out, not_932_out, not_933_out);
  and and_294 (and_294_out, not_934_out, Entrada6, not_935_out, not_936_out, not_937_out, not_938_out);
  and and_295 (and_295_out, not_939_out, Entrada6, not_940_out, not_941_out, Entrada2, Entrada1);
  and and_296 (and_296_out, not_942_out, Entrada6, not_943_out, not_944_out, Entrada3, not_945_out);
  and and_297 (and_297_out, not_946_out, not_947_out, Entrada6, Entrada4, not_948_out, Entrada2);
  and and_298 (and_298_out, not_949_out, Entrada6, Entrada4, Entrada2, not_950_out);
  and and_299 (and_299_out, not_951_out, not_952_out, Entrada6, Entrada5, not_953_out, Entrada3, Entrada1);
  and and_300 (and_300_out, not_954_out, not_955_out, Entrada6, Entrada5, Entrada4, Entrada2);
  and and_301 (and_301_out, not_956_out, Entrada6, Entrada5, Entrada4, not_957_out, Entrada2);
  and and_302 (and_302_out, not_958_out, Entrada7, not_959_out, not_960_out, not_961_out, not_962_out, Entrada1);
  and and_303 (and_303_out, not_963_out, Entrada7, not_964_out, Entrada3, not_965_out);
  and and_304 (and_304_out, Entrada7, not_966_out, not_967_out, Entrada3, not_968_out);
  and and_305 (and_305_out, not_969_out, Entrada7, not_970_out, not_971_out, Entrada3, not_972_out, Entrada1);
  and and_306 (and_306_out, not_973_out, Entrada7, not_974_out, Entrada4, not_975_out, not_976_out);
  and and_307 (and_307_out, not_977_out, Entrada7, not_978_out, not_979_out, Entrada4, Entrada2, Entrada1);
  and and_308 (and_308_out, Entrada7, not_980_out, Entrada5, not_981_out, not_982_out);
  and and_309 (and_309_out, Entrada7, Entrada5, not_983_out, not_984_out, not_985_out);
  and and_310 (and_310_out, not_986_out, Entrada7, not_987_out, Entrada5, Entrada4, Entrada3, Entrada1);
  and and_311 (and_311_out, not_988_out, Entrada7, Entrada6, not_989_out, not_990_out, not_991_out);
  and and_312 (and_312_out, not_992_out, Entrada7, Entrada6, not_993_out, Entrada3, Entrada2);
  and and_313 (and_313_out, not_994_out, Entrada7, Entrada6, not_995_out, Entrada4, not_996_out, Entrada1);
  and and_314 (and_314_out, not_997_out, Entrada7, Entrada6, Entrada4, Entrada3, not_998_out, Entrada1);
  and and_315 (and_315_out, not_999_out, Entrada7, Entrada6, Entrada5, not_1000_out, not_1001_out, Entrada1);
  and and_316 (and_316_out, Entrada8, not_1002_out, not_1003_out, not_1004_out, not_1005_out, not_1006_out);
  and and_317 (and_317_out, Entrada8, not_1007_out, not_1008_out, not_1009_out, not_1010_out);
  and and_318 (and_318_out, Entrada8, not_1011_out, not_1012_out, not_1013_out, not_1014_out, Entrada1);
  and and_319 (and_319_out, Entrada8, not_1015_out, not_1016_out, not_1017_out, not_1018_out, Entrada3, Entrada1);
  and and_320 (and_320_out, Entrada8, not_1019_out, not_1020_out, not_1021_out, Entrada3, not_1022_out, Entrada1);
  and and_321 (and_321_out, Entrada8, not_1023_out, Entrada4, not_1024_out, not_1025_out, not_1026_out);
  and and_322 (and_322_out, Entrada8, not_1027_out, not_1028_out, Entrada4, not_1029_out, Entrada2);
  and and_323 (and_323_out, Entrada8, not_1030_out, not_1031_out, Entrada4, Entrada2, not_1032_out);
  and and_324 (and_324_out, Entrada8, not_1033_out, not_1034_out, Entrada4, Entrada2, Entrada1);
  and and_325 (and_325_out, Entrada8, not_1035_out, Entrada5, Entrada3, not_1036_out);
  and and_326 (and_326_out, Entrada8, not_1037_out, Entrada6, not_1038_out, not_1039_out, Entrada2);
  and and_327 (and_327_out, Entrada8, not_1040_out, Entrada6, not_1041_out, Entrada2, not_1042_out);
  and and_328 (and_328_out, Entrada8, Entrada6, not_1043_out, Entrada2, not_1044_out);
  and and_329 (and_329_out, Entrada8, Entrada6, not_1045_out, Entrada4, not_1046_out, not_1047_out);
  and and_330 (and_330_out, Entrada8, not_1048_out, Entrada6, Entrada4, not_1049_out, Entrada1);
  and and_331 (and_331_out, Entrada8, not_1050_out, Entrada6, not_1051_out, Entrada4, Entrada3, Entrada1);
  and and_332 (and_332_out, Entrada8, not_1052_out, Entrada6, Entrada5, not_1053_out, Entrada2);
  and and_333 (and_333_out, Entrada8, Entrada6, Entrada5, not_1054_out, not_1055_out, Entrada2);
  and and_334 (and_334_out, Entrada8, Entrada7, not_1056_out, not_1057_out, not_1058_out, not_1059_out);
  and and_335 (and_335_out, Entrada8, Entrada7, not_1060_out, not_1061_out, not_1062_out, Entrada2, Entrada1);
  and and_336 (and_336_out, Entrada8, Entrada7, not_1063_out, not_1064_out, Entrada4, Entrada3, not_1065_out, Entrada1);
  and and_337 (and_337_out, Entrada8, Entrada7, not_1066_out, Entrada5, not_1067_out, not_1068_out);
  and and_338 (and_338_out, Entrada8, Entrada7, not_1069_out, Entrada5, not_1070_out, not_1071_out);
  and and_339 (and_339_out, Entrada8, Entrada7, Entrada5, not_1072_out, not_1073_out);
  and and_340 (and_340_out, Entrada8, Entrada7, not_1074_out, Entrada5, not_1075_out, Entrada3, Entrada1);
  and and_341 (and_341_out, Entrada8, Entrada7, not_1076_out, Entrada5, Entrada4, Entrada2);
  and and_342 (and_342_out, Entrada8, Entrada7, Entrada6, not_1077_out, not_1078_out, not_1079_out, Entrada1);
  and and_343 (and_343_out, Entrada8, Entrada7, Entrada6, not_1080_out, Entrada3, not_1081_out, Entrada1);
  and and_344 (and_344_out, Entrada8, Entrada7, Entrada6, not_1082_out, Entrada4, not_1083_out, Entrada1);
  and and_345 (and_345_out, Entrada8, Entrada7, Entrada6, not_1084_out, Entrada4, Entrada3, Entrada2);
  and and_346 (and_346_out, Entrada8, Entrada7, Entrada6, Entrada5, Entrada4, not_1085_out);
  and and_347 (and_347_out, Entrada8, Entrada7, Entrada6, Entrada5, Entrada4, Entrada3, Entrada1);
  and and_348 (and_348_out, not_1086_out, not_1087_out, not_1088_out, not_1089_out);
  and and_349 (and_349_out, not_1090_out, not_1091_out, not_1092_out, not_1093_out, not_1094_out);
  and and_350 (and_350_out, not_1095_out, not_1096_out, not_1097_out, not_1098_out, Entrada3);
  and and_351 (and_351_out, not_1099_out, not_1100_out, Entrada4, Entrada2);
  and and_352 (and_352_out, not_1101_out, not_1102_out, Entrada5, not_1103_out);
  and and_353 (and_353_out, not_1104_out, Entrada5, not_1105_out, not_1106_out);
  and and_354 (and_354_out, not_1107_out, not_1108_out, Entrada5, Entrada3, not_1109_out);
  and and_355 (and_355_out, not_1110_out, not_1111_out, Entrada6, not_1112_out, Entrada2);
  and and_356 (and_356_out, not_1113_out, Entrada6, Entrada4, not_1114_out);
  and and_357 (and_357_out, not_1115_out, Entrada6, not_1116_out, Entrada4, Entrada3);
  and and_358 (and_358_out, not_1117_out, Entrada6, Entrada5, not_1118_out, Entrada2);
  and and_359 (and_359_out, not_1119_out, Entrada7, not_1120_out, not_1121_out, not_1122_out);
  and and_360 (and_360_out, Entrada7, not_1123_out, not_1124_out, Entrada3);
  and and_361 (and_361_out, Entrada7, not_1125_out, Entrada3, not_1126_out);
  and and_362 (and_362_out, Entrada7, not_1127_out, Entrada5, not_1128_out, not_1129_out);
  and and_363 (and_363_out, not_1130_out, Entrada7, Entrada5, not_1131_out, Entrada3);
  and and_364 (and_364_out, Entrada7, Entrada6, not_1132_out, not_1133_out, Entrada2);
  and and_365 (and_365_out, Entrada7, Entrada6, Entrada5, Entrada3, Entrada2);
  and and_366 (and_366_out, Entrada8, not_1134_out, not_1135_out, not_1136_out, Entrada2);
  and and_367 (and_367_out, Entrada8, not_1137_out, not_1138_out, Entrada2);
  and and_368 (and_368_out, Entrada8, not_1139_out, not_1140_out, Entrada4, not_1141_out);
  and and_369 (and_369_out, Entrada8, not_1142_out, Entrada4, Entrada3, not_1143_out);
  and and_370 (and_370_out, Entrada8, not_1144_out, Entrada5, Entrada4, Entrada3);
  and and_371 (and_371_out, Entrada8, not_1145_out, Entrada6, not_1146_out, not_1147_out);
  and and_372 (and_372_out, Entrada8, Entrada6, not_1148_out, not_1149_out);
  and and_373 (and_373_out, Entrada8, Entrada6, not_1150_out, not_1151_out, Entrada3);
  and and_374 (and_374_out, Entrada8, Entrada6, Entrada4, Entrada2);
  and and_375 (and_375_out, Entrada8, Entrada7, Entrada5, Entrada4, not_1152_out);
  or or_1 (or_1_out, and_241_out, and_242_out, and_243_out, and_244_out, and_245_out, and_246_out, and_247_out, and_248_out, and_249_out, and_250_out, and_251_out, and_252_out, and_253_out, and_254_out, and_255_out, and_256_out, and_257_out);
  or or_2 (or_2_out, and_258_out, and_259_out, and_260_out, and_261_out, and_262_out, and_263_out, and_264_out, and_265_out, and_266_out, and_267_out, and_268_out, and_269_out, and_270_out, and_271_out, and_272_out, and_273_out, and_274_out);
  or or_3 (or_3_out, and_1_out, and_2_out, and_3_out, and_4_out, and_5_out, and_6_out, and_7_out, and_8_out, and_9_out, and_10_out, and_11_out, and_12_out, and_13_out, and_14_out, and_15_out, and_16_out, and_17_out, and_18_out, and_19_out, and_20_out, and_21_out, and_22_out, and_23_out, and_24_out, and_25_out, and_26_out, and_27_out, and_28_out);
  or or_4 (or_4_out, and_29_out, and_30_out, and_31_out, and_32_out, and_33_out, and_34_out, and_35_out, and_36_out, and_37_out, and_38_out, and_39_out, and_40_out, and_41_out, and_42_out, and_43_out, and_44_out, and_45_out, and_46_out, and_47_out, and_48_out, and_49_out, and_50_out, and_51_out, and_52_out, and_53_out, and_54_out, and_55_out, and_56_out);
  or or_5 (or_5_out, and_57_out, and_58_out, and_59_out, and_60_out, and_61_out, and_62_out, and_63_out, and_64_out, and_65_out, and_66_out, and_67_out, and_68_out, and_69_out, and_70_out, and_71_out, and_72_out, and_73_out, and_74_out, and_75_out, and_76_out, and_77_out, and_78_out, and_79_out, and_80_out, and_81_out, and_82_out, and_83_out, and_84_out, and_85_out);
  or or_6 (or_6_out, and_86_out, and_87_out, and_88_out, and_89_out, and_90_out, and_91_out, and_92_out, and_93_out, and_94_out, and_95_out, and_96_out, and_97_out, and_98_out, and_99_out, and_100_out, and_101_out, and_102_out, and_103_out, and_104_out, and_105_out, and_106_out, and_107_out, and_108_out, and_109_out, and_110_out, and_111_out, and_112_out, and_113_out);
  or or_7 (or_7_out, and_114_out, and_115_out, and_116_out, and_117_out, and_118_out, and_119_out, and_120_out, and_121_out, and_122_out, and_123_out, and_124_out, and_125_out, and_126_out, and_127_out, and_128_out, and_129_out, and_130_out, and_131_out, and_132_out, and_133_out, and_134_out, and_135_out, and_136_out, and_137_out, and_138_out, and_139_out, and_140_out, and_141_out, and_142_out, and_143_out, and_144_out, and_145_out);
  or or_8 (or_8_out, and_146_out, and_147_out, and_148_out, and_149_out, and_150_out, and_151_out, and_152_out, and_153_out, and_154_out, and_155_out, and_156_out, and_157_out, and_158_out, and_159_out, and_160_out, and_161_out, and_162_out, and_163_out, and_164_out, and_165_out, and_166_out, and_167_out, and_168_out, and_169_out, and_170_out, and_171_out, and_172_out, and_173_out, and_174_out, and_175_out, and_176_out, and_177_out);
  or or_9 (or_9_out, and_178_out, and_179_out, and_180_out, and_181_out, and_182_out, and_183_out, and_184_out, and_185_out, and_186_out, and_187_out, and_188_out, and_189_out, and_190_out, and_191_out, and_192_out, and_193_out, and_194_out, and_195_out, and_196_out, and_197_out, and_198_out, and_199_out, and_200_out, and_201_out, and_202_out, and_203_out, and_204_out, and_205_out, and_206_out, and_207_out, and_208_out, and_209_out);
  or or_10 (or_10_out, and_210_out, and_211_out, and_212_out, and_213_out, and_214_out, and_215_out, and_216_out, and_217_out, and_218_out, and_219_out, and_220_out, and_221_out, and_222_out, and_223_out, and_224_out, and_225_out, and_226_out, and_227_out, and_228_out, and_229_out, and_230_out, and_231_out, and_232_out, and_233_out, and_234_out, and_235_out, and_236_out, and_237_out, and_238_out, and_239_out, and_240_out);
  or or_11 (S5, or_1_out, or_2_out);
  or or_12 (or_12_out, and_275_out, and_276_out, and_277_out, and_278_out, and_279_out, and_280_out, and_281_out, and_282_out, and_283_out, and_284_out, and_285_out, and_286_out, and_287_out, and_288_out, and_289_out, and_290_out, and_291_out, and_292_out, and_293_out, and_294_out, and_295_out, and_296_out, and_297_out, and_298_out, and_299_out);
  or or_13 (or_13_out, and_300_out, and_301_out, and_302_out, and_303_out, and_304_out, and_305_out, and_306_out, and_307_out, and_308_out, and_309_out, and_310_out, and_311_out, and_312_out, and_313_out, and_314_out, and_315_out, and_316_out, and_317_out, and_318_out, and_319_out, and_320_out, and_321_out, and_322_out, and_323_out);
  or or_14 (or_14_out, and_324_out, and_325_out, and_326_out, and_327_out, and_328_out, and_329_out, and_330_out, and_331_out, and_332_out, and_333_out, and_334_out, and_335_out, and_336_out, and_337_out, and_338_out, and_339_out, and_340_out, and_341_out, and_342_out, and_343_out, and_344_out, and_345_out, and_346_out, and_347_out);
  or or_15 (S7, and_348_out, and_349_out, Entrada1, and_350_out, and_351_out, and_352_out, and_353_out, and_354_out, and_355_out, and_356_out, and_357_out, and_358_out, and_359_out, and_360_out, and_361_out, and_362_out, and_363_out, and_364_out, and_365_out, and_366_out, and_367_out, and_368_out, and_369_out, and_370_out, and_371_out, and_372_out, and_373_out, and_374_out, and_375_out);
  or or_16 (S1, or_3_out, or_4_out);
  or or_17 (S2, or_5_out, or_6_out);
  or or_18 (S3, or_7_out, or_8_out);
  or or_19 (S4, or_9_out, or_10_out);
  or or_20 (S6, or_12_out, or_13_out, or_14_out);
endmodule

module Dezenas (
  input  E1,
  input  E2,
  input  E3,
  input  E4,
  input  E5,
  input  E6,
  input  E7,
  input  E8,
  output S1,
  output S2,
  output S3,
  output S4,
  output S5,
  output S6,
  output S7
);

  wire and_1_out, and_2_out, and_3_out, and_4_out, and_5_out, and_6_out, and_7_out, and_8_out, and_9_out,
       and_10_out, and_11_out, and_12_out, and_13_out, and_14_out, and_15_out, and_16_out, and_17_out,
       and_18_out, and_19_out, and_20_out, and_21_out, and_22_out, and_23_out, and_24_out, and_25_out,
       and_26_out, and_27_out, and_28_out, and_29_out, and_30_out, and_31_out, and_32_out, and_33_out,
       and_34_out, and_35_out, and_36_out, and_37_out, and_38_out, and_39_out, and_40_out, and_41_out,
       and_42_out, and_43_out, and_44_out, and_45_out, and_46_out, and_47_out, and_48_out, and_49_out,
       and_50_out, and_51_out, and_52_out, and_53_out, and_54_out, and_55_out, and_56_out, and_57_out,
       and_58_out, and_59_out, and_60_out, and_61_out, and_62_out, and_63_out, and_64_out, and_65_out,
       and_66_out, and_67_out, and_68_out, and_69_out, and_70_out, and_71_out, and_72_out, and_73_out,
       and_74_out, and_75_out, and_76_out, and_77_out, and_78_out, and_79_out, and_80_out, and_81_out,
       and_82_out, and_83_out, and_84_out, and_85_out, and_86_out, and_87_out, and_88_out, and_89_out,
       and_90_out, and_91_out, and_92_out, and_93_out, and_94_out, and_95_out, and_96_out, and_97_out,
       and_98_out, and_99_out, and_100_out, and_101_out, and_102_out, and_103_out, and_104_out, and_105_out,
       and_106_out, and_107_out, and_108_out, and_109_out, and_110_out, and_111_out, and_112_out,
       and_113_out, and_114_out, and_115_out, and_116_out, not_1_out, not_2_out, not_3_out, not_4_out,
       not_5_out, not_6_out, not_7_out, not_8_out, not_9_out, not_10_out, not_11_out, not_12_out, not_13_out,
       not_14_out, not_15_out, not_16_out, not_17_out, not_18_out, not_19_out, not_20_out, not_21_out,
       not_22_out, not_23_out, not_24_out, not_25_out, not_26_out, not_27_out, not_28_out, not_29_out,
       not_30_out, not_31_out, not_32_out, not_33_out, not_34_out, not_35_out, not_36_out, not_37_out,
       not_38_out, not_39_out, not_40_out, not_41_out, not_42_out, not_43_out, not_44_out, not_45_out,
       not_46_out, not_47_out, not_48_out, not_49_out, not_50_out, not_51_out, not_52_out, not_53_out,
       not_54_out, not_55_out, not_56_out, not_57_out, not_58_out, not_59_out, not_60_out, not_61_out,
       not_62_out, not_63_out, not_64_out, not_65_out, not_66_out, not_67_out, not_68_out, not_69_out,
       not_70_out, not_71_out, not_72_out, not_73_out, not_74_out, not_75_out, not_76_out, not_77_out,
       not_78_out, not_79_out, not_80_out, not_81_out, not_82_out, not_83_out, not_84_out, not_85_out,
       not_86_out, not_87_out, not_88_out, not_89_out, not_90_out, not_91_out, not_92_out, not_93_out,
       not_94_out, not_95_out, not_96_out, not_97_out, not_98_out, not_99_out, not_100_out, not_101_out,
       not_102_out, not_103_out, not_104_out, not_105_out, not_106_out, not_107_out, not_108_out,
       not_109_out, not_110_out, not_111_out, not_112_out, not_113_out, not_114_out, not_115_out,
       not_116_out, not_117_out, not_118_out, not_119_out, not_120_out, not_121_out, not_122_out,
       not_123_out, not_124_out, not_125_out, not_126_out, not_127_out, not_128_out, not_129_out,
       not_130_out, not_131_out, not_132_out, not_133_out, not_134_out, not_135_out, not_136_out,
       not_137_out, not_138_out, not_139_out, not_140_out, not_141_out, not_142_out, not_143_out,
       not_144_out, not_145_out, not_146_out, not_147_out, not_148_out, not_149_out, not_150_out,
       not_151_out, not_152_out, not_153_out, not_154_out, not_155_out, not_156_out, not_157_out,
       not_158_out, not_159_out, not_160_out, not_161_out, not_162_out, not_163_out, not_164_out,
       not_165_out, not_166_out, not_167_out, not_168_out, not_169_out, not_170_out, not_171_out,
       not_172_out, not_173_out, not_174_out, not_175_out, not_176_out, not_177_out, not_178_out,
       not_179_out, not_180_out, not_181_out, not_182_out, not_183_out, not_184_out, not_185_out,
       not_186_out, not_187_out, not_188_out, not_189_out, not_190_out, not_191_out, not_192_out,
       not_193_out, not_194_out, not_195_out, not_196_out, not_197_out, not_198_out, not_199_out,
       not_200_out, not_201_out, not_202_out, not_203_out, not_204_out, not_205_out, not_206_out,
       not_207_out, not_208_out, not_209_out, not_210_out, not_211_out, not_212_out, not_213_out,
       not_214_out, not_215_out, not_216_out, not_217_out, not_218_out, not_219_out, not_220_out,
       not_221_out, not_222_out, not_223_out, not_224_out, not_225_out, not_226_out, not_227_out,
       not_228_out, not_229_out, not_230_out, not_231_out, not_232_out, not_233_out, not_234_out,
       not_235_out, not_236_out, not_237_out, not_238_out, not_239_out, not_240_out, not_241_out,
       not_242_out, not_243_out, not_244_out, not_245_out, not_246_out, not_247_out, not_248_out,
       not_249_out, not_250_out, not_251_out, not_252_out, not_253_out, not_254_out, not_255_out,
       not_256_out, not_257_out, not_258_out, not_259_out, not_260_out, not_261_out, not_262_out,
       not_263_out, not_264_out, not_265_out, not_266_out, not_267_out, not_268_out;

  not not_1 (not_1_out, E2);
  not not_2 (not_2_out, E1);
  not not_3 (not_3_out, E2);
  not not_4 (not_4_out, E1);
  not not_5 (not_5_out, E2);
  not not_6 (not_6_out, E3);
  not not_7 (not_7_out, E4);
  not not_8 (not_8_out, E5);
  not not_9 (not_9_out, E7);
  not not_10 (not_10_out, E4);
  not not_11 (not_11_out, E5);
  not not_12 (not_12_out, E6);
  not not_13 (not_13_out, E1);
  not not_14 (not_14_out, E3);
  not not_15 (not_15_out, E2);
  not not_16 (not_16_out, E3);
  not not_17 (not_17_out, E2);
  not not_18 (not_18_out, E4);
  not not_19 (not_19_out, E6);
  not not_20 (not_20_out, E7);
  not not_21 (not_21_out, E4);
  not not_22 (not_22_out, E5);
  not not_23 (not_23_out, E1);
  not not_24 (not_24_out, E2);
  not not_25 (not_25_out, E3);
  not not_26 (not_26_out, E4);
  not not_27 (not_27_out, E5);
  not not_28 (not_28_out, E1);
  not not_29 (not_29_out, E2);
  not not_30 (not_30_out, E3);
  not not_31 (not_31_out, E4);
  not not_32 (not_32_out, E6);
  not not_33 (not_33_out, E7);
  not not_34 (not_34_out, E1);
  not not_35 (not_35_out, E3);
  not not_36 (not_36_out, E4);
  not not_37 (not_37_out, E5);
  not not_38 (not_38_out, E6);
  not not_39 (not_39_out, E1);
  not not_40 (not_40_out, E3);
  not not_41 (not_41_out, E4);
  not not_42 (not_42_out, E5);
  not not_43 (not_43_out, E7);
  not not_44 (not_44_out, E1);
  not not_45 (not_45_out, E2);
  not not_46 (not_46_out, E2);
  not not_47 (not_47_out, E6);
  not not_48 (not_48_out, E7);
  not not_49 (not_49_out, E1);
  not not_50 (not_50_out, E2);
  not not_51 (not_51_out, E3);
  not not_52 (not_52_out, E5);
  not not_53 (not_53_out, E6);
  not not_54 (not_54_out, E7);
  not not_55 (not_55_out, E1);
  not not_56 (not_56_out, E3);
  not not_57 (not_57_out, E1);
  not not_58 (not_58_out, E4);
  not not_59 (not_59_out, E5);
  not not_60 (not_60_out, E1);
  not not_61 (not_61_out, E4);
  not not_62 (not_62_out, E6);
  not not_63 (not_63_out, E1);
  not not_64 (not_64_out, E4);
  not not_65 (not_65_out, E7);
  not not_66 (not_66_out, E3);
  not not_67 (not_67_out, E4);
  not not_68 (not_68_out, E2);
  not not_69 (not_69_out, E3);
  not not_70 (not_70_out, E2);
  not not_71 (not_71_out, E2);
  not not_72 (not_72_out, E2);
  not not_73 (not_73_out, E4);
  not not_74 (not_74_out, E5);
  not not_75 (not_75_out, E3);
  not not_76 (not_76_out, E4);
  not not_77 (not_77_out, E3);
  not not_78 (not_78_out, E4);
  not not_79 (not_79_out, E6);
  not not_80 (not_80_out, E7);
  not not_81 (not_81_out, E4);
  not not_82 (not_82_out, E5);
  not not_83 (not_83_out, E1);
  not not_84 (not_84_out, E2);
  not not_85 (not_85_out, E5);
  not not_86 (not_86_out, E2);
  not not_87 (not_87_out, E5);
  not not_88 (not_88_out, E2);
  not not_89 (not_89_out, E2);
  not not_90 (not_90_out, E5);
  not not_91 (not_91_out, E1);
  not not_92 (not_92_out, E3);
  not not_93 (not_93_out, E3);
  not not_94 (not_94_out, E5);
  not not_95 (not_95_out, E6);
  not not_96 (not_96_out, E7);
  not not_97 (not_97_out, E4);
  not not_98 (not_98_out, E7);
  not not_99 (not_99_out, E1);
  not not_100 (not_100_out, E6);
  not not_101 (not_101_out, E4);
  not not_102 (not_102_out, E6);
  not not_103 (not_103_out, E2);
  not not_104 (not_104_out, E4);
  not not_105 (not_105_out, E2);
  not not_106 (not_106_out, E3);
  not not_107 (not_107_out, E4);
  not not_108 (not_108_out, E2);
  not not_109 (not_109_out, E3);
  not not_110 (not_110_out, E5);
  not not_111 (not_111_out, E6);
  not not_112 (not_112_out, E2);
  not not_113 (not_113_out, E3);
  not not_114 (not_114_out, E5);
  not not_115 (not_115_out, E7);
  not not_116 (not_116_out, E3);
  not not_117 (not_117_out, E4);
  not not_118 (not_118_out, E4);
  not not_119 (not_119_out, E4);
  not not_120 (not_120_out, E1);
  not not_121 (not_121_out, E3);
  not not_122 (not_122_out, E5);
  not not_123 (not_123_out, E6);
  not not_124 (not_124_out, E7);
  not not_125 (not_125_out, E1);
  not not_126 (not_126_out, E4);
  not not_127 (not_127_out, E4);
  not not_128 (not_128_out, E1);
  not not_129 (not_129_out, E5);
  not not_130 (not_130_out, E6);
  not not_131 (not_131_out, E7);
  not not_132 (not_132_out, E2);
  not not_133 (not_133_out, E3);
  not not_134 (not_134_out, E1);
  not not_135 (not_135_out, E2);
  not not_136 (not_136_out, E3);
  not not_137 (not_137_out, E4);
  not not_138 (not_138_out, E6);
  not not_139 (not_139_out, E7);
  not not_140 (not_140_out, E1);
  not not_141 (not_141_out, E3);
  not not_142 (not_142_out, E4);
  not not_143 (not_143_out, E5);
  not not_144 (not_144_out, E6);
  not not_145 (not_145_out, E2);
  not not_146 (not_146_out, E3);
  not not_147 (not_147_out, E4);
  not not_148 (not_148_out, E5);
  not not_149 (not_149_out, E6);
  not not_150 (not_150_out, E7);
  not not_151 (not_151_out, E1);
  not not_152 (not_152_out, E2);
  not not_153 (not_153_out, E3);
  not not_154 (not_154_out, E5);
  not not_155 (not_155_out, E1);
  not not_156 (not_156_out, E3);
  not not_157 (not_157_out, E5);
  not not_158 (not_158_out, E7);
  not not_159 (not_159_out, E1);
  not not_160 (not_160_out, E2);
  not not_161 (not_161_out, E3);
  not not_162 (not_162_out, E6);
  not not_163 (not_163_out, E1);
  not not_164 (not_164_out, E2);
  not not_165 (not_165_out, E3);
  not not_166 (not_166_out, E7);
  not not_167 (not_167_out, E1);
  not not_168 (not_168_out, E1);
  not not_169 (not_169_out, E3);
  not not_170 (not_170_out, E5);
  not not_171 (not_171_out, E1);
  not not_172 (not_172_out, E3);
  not not_173 (not_173_out, E6);
  not not_174 (not_174_out, E7);
  not not_175 (not_175_out, E3);
  not not_176 (not_176_out, E5);
  not not_177 (not_177_out, E6);
  not not_178 (not_178_out, E7);
  not not_179 (not_179_out, E1);
  not not_180 (not_180_out, E4);
  not not_181 (not_181_out, E5);
  not not_182 (not_182_out, E1);
  not not_183 (not_183_out, E6);
  not not_184 (not_184_out, E1);
  not not_185 (not_185_out, E7);
  not not_186 (not_186_out, E2);
  not not_187 (not_187_out, E4);
  not not_188 (not_188_out, E6);
  not not_189 (not_189_out, E7);
  not not_190 (not_190_out, E4);
  not not_191 (not_191_out, E5);
  not not_192 (not_192_out, E6);
  not not_193 (not_193_out, E4);
  not not_194 (not_194_out, E5);
  not not_195 (not_195_out, E7);
  not not_196 (not_196_out, E2);
  not not_197 (not_197_out, E5);
  not not_198 (not_198_out, E2);
  not not_199 (not_199_out, E6);
  not not_200 (not_200_out, E2);
  not not_201 (not_201_out, E7);
  not not_202 (not_202_out, E3);
  not not_203 (not_203_out, E4);
  not not_204 (not_204_out, E3);
  not not_205 (not_205_out, E2);
  not not_206 (not_206_out, E3);
  not not_207 (not_207_out, E4);
  not not_208 (not_208_out, E6);
  not not_209 (not_209_out, E7);
  not not_210 (not_210_out, E2);
  not not_211 (not_211_out, E4);
  not not_212 (not_212_out, E5);
  not not_213 (not_213_out, E4);
  not not_214 (not_214_out, E5);
  not not_215 (not_215_out, E6);
  not not_216 (not_216_out, E4);
  not not_217 (not_217_out, E5);
  not not_218 (not_218_out, E7);
  not not_219 (not_219_out, E1);
  not not_220 (not_220_out, E2);
  not not_221 (not_221_out, E5);
  not not_222 (not_222_out, E2);
  not not_223 (not_223_out, E5);
  not not_224 (not_224_out, E2);
  not not_225 (not_225_out, E4);
  not not_226 (not_226_out, E5);
  not not_227 (not_227_out, E1);
  not not_228 (not_228_out, E2);
  not not_229 (not_229_out, E5);
  not not_230 (not_230_out, E2);
  not not_231 (not_231_out, E5);
  not not_232 (not_232_out, E3);
  not not_233 (not_233_out, E5);
  not not_234 (not_234_out, E6);
  not not_235 (not_235_out, E7);
  not not_236 (not_236_out, E1);
  not not_237 (not_237_out, E3);
  not not_238 (not_238_out, E4);
  not not_239 (not_239_out, E7);
  not not_240 (not_240_out, E1);
  not not_241 (not_241_out, E6);
  not not_242 (not_242_out, E3);
  not not_243 (not_243_out, E4);
  not not_244 (not_244_out, E6);
  not not_245 (not_245_out, E4);
  not not_246 (not_246_out, E6);
  not not_247 (not_247_out, E7);
  not not_248 (not_248_out, E4);
  not not_249 (not_249_out, E1);
  not not_250 (not_250_out, E4);
  not not_251 (not_251_out, E1);
  not not_252 (not_252_out, E5);
  not not_253 (not_253_out, E6);
  not not_254 (not_254_out, E3);
  not not_255 (not_255_out, E4);
  not not_256 (not_256_out, E4);
  not not_257 (not_257_out, E4);
  not not_258 (not_258_out, E2);
  not not_259 (not_259_out, E2);
  not not_260 (not_260_out, E1);
  not not_261 (not_261_out, E3);
  not not_262 (not_262_out, E1);
  not not_263 (not_263_out, E5);
  not not_264 (not_264_out, E3);
  not not_265 (not_265_out, E4);
  not not_266 (not_266_out, E2);
  not not_267 (not_267_out, E6);
  not not_268 (not_268_out, E5);
  and and_1 (and_1_out, not_1_out, E4, E6);
  and and_2 (and_2_out, not_2_out, E4, E5);
  and and_3 (and_3_out, not_3_out, E4, E5);
  and and_4 (and_4_out, E4, E5, E6);
  and and_5 (and_5_out, not_4_out, not_5_out, E3);
  and and_6 (and_6_out, E2, not_6_out, not_7_out, not_8_out, not_9_out);
  and and_7 (and_7_out, E2, not_10_out, not_11_out, not_12_out);
  and and_8 (and_8_out, not_13_out, E2, not_14_out, E4);
  and and_9 (and_9_out, E1, not_15_out, not_16_out);
  and and_10 (and_10_out, E1, not_17_out, not_18_out, not_19_out, not_20_out);
  and and_11 (and_11_out, E1, not_21_out, not_22_out);
  and and_12 (and_12_out, E1, E2, E3);
  and and_13 (and_13_out, not_23_out, not_24_out, not_25_out, not_26_out, not_27_out);
  and and_14 (and_14_out, not_28_out, not_29_out, not_30_out, not_31_out, not_32_out, not_33_out);
  and and_15 (and_15_out, not_34_out, not_35_out, not_36_out, not_37_out, not_38_out);
  and and_16 (and_16_out, not_39_out, not_40_out, not_41_out, not_42_out, not_43_out);
  and and_17 (and_17_out, not_44_out, not_45_out, E3, E5);
  and and_18 (and_18_out, not_46_out, E3, E5, not_47_out, not_48_out);
  and and_19 (and_19_out, not_49_out, not_50_out, E3, E4);
  and and_20 (and_20_out, E2, not_51_out, not_52_out, not_53_out, not_54_out);
  and and_21 (and_21_out, not_55_out, E2, not_56_out, E4);
  and and_22 (and_22_out, not_57_out, E2, E3, not_58_out, not_59_out);
  and and_23 (and_23_out, not_60_out, E2, E3, not_61_out, not_62_out);
  and and_24 (and_24_out, not_63_out, E2, E3, not_64_out, not_65_out);
  and and_25 (and_25_out, E1, not_66_out, not_67_out, E5, E6);
  and and_26 (and_26_out, E1, not_68_out, not_69_out, E4);
  and and_27 (and_27_out, E1, not_70_out, E4, E6);
  and and_28 (and_28_out, E1, not_71_out, E4, E5);
  and and_29 (and_29_out, E1, not_72_out, E3, not_73_out, not_74_out);
  and and_30 (and_30_out, E1, E2, not_75_out, not_76_out);
  and and_31 (and_31_out, E1, E2, E3, E4);
  and and_32 (and_32_out, not_77_out, not_78_out, not_79_out, not_80_out);
  and and_33 (and_33_out, not_81_out, not_82_out);
  and and_34 (and_34_out, not_83_out, not_84_out, not_85_out, E6);
  and and_35 (and_35_out, not_86_out, not_87_out, E6, E7);
  and and_36 (and_36_out, not_88_out, E4, E5);
  and and_37 (and_37_out, E4, E5, E6);
  and and_38 (and_38_out, not_89_out, E3, not_90_out, E7);
  and and_39 (and_39_out, E3, E4, E5, E7);
  and and_40 (and_40_out, not_91_out, E2, not_92_out);
  and and_41 (and_41_out, E2, not_93_out, not_94_out, not_95_out, not_96_out);
  and and_42 (and_42_out, E2, not_97_out, not_98_out);
  and and_43 (and_43_out, not_99_out, E2, E5, not_100_out);
  and and_44 (and_44_out, E1, not_101_out, not_102_out);
  and and_45 (and_45_out, E1, not_103_out, E3);
  and and_46 (and_46_out, E1, E2, not_104_out);
  and and_47 (and_47_out, not_105_out, not_106_out, not_107_out);
  and and_48 (and_48_out, not_108_out, not_109_out, not_110_out, not_111_out);
  and and_49 (and_49_out, not_112_out, not_113_out, not_114_out, not_115_out);
  and and_50 (and_50_out, not_116_out, not_117_out, E6, E7);
  and and_51 (and_51_out, not_118_out, E5, E7);
  and and_52 (and_52_out, not_119_out, E5, E6);
  and and_53 (and_53_out, not_120_out, not_121_out, E4);
  and and_54 (and_54_out, E4, not_122_out, not_123_out, not_124_out);
  and and_55 (and_55_out, not_125_out, E3, not_126_out);
  and and_56 (and_56_out, E2, not_127_out, E5);
  and and_57 (and_57_out, not_128_out, E2, E4);
  and and_58 (and_58_out, E2, E3, not_129_out);
  and and_59 (and_59_out, E2, E3, not_130_out, not_131_out);
  and and_60 (and_60_out, E1, not_132_out, E3, E4);
  and and_61 (and_61_out, E1, E2, not_133_out);
  and and_62 (and_62_out, not_134_out, not_135_out, not_136_out, not_137_out, not_138_out, not_139_out);
  and and_63 (and_63_out, not_140_out, not_141_out, not_142_out, not_143_out, not_144_out);
  and and_64 (and_64_out, not_145_out, not_146_out, not_147_out, not_148_out, not_149_out, not_150_out);
  and and_65 (and_65_out, not_151_out, not_152_out, not_153_out, not_154_out, E6);
  and and_66 (and_66_out, not_155_out, not_156_out, not_157_out, E6, not_158_out);
  and and_67 (and_67_out, not_159_out, not_160_out, not_161_out, E4, E5, not_162_out);
  and and_68 (and_68_out, not_163_out, not_164_out, not_165_out, E4, E5, not_166_out);
  and and_69 (and_69_out, not_167_out, E3, E4, E5, E6);
  and and_70 (and_70_out, not_168_out, E2, not_169_out, E4, not_170_out);
  and and_71 (and_71_out, not_171_out, E2, not_172_out, E4, not_173_out, not_174_out);
  and and_72 (and_72_out, E2, not_175_out, E4, not_176_out, not_177_out, not_178_out);
  and and_73 (and_73_out, not_179_out, E2, E3, not_180_out, not_181_out, E6);
  and and_74 (and_74_out, not_182_out, E2, E3, E5, not_183_out);
  and and_75 (and_75_out, not_184_out, E2, E3, E5, not_185_out);
  and and_76 (and_76_out, E1, not_186_out, E3, not_187_out, not_188_out, not_189_out);
  and and_77 (and_77_out, E1, E3, not_190_out, not_191_out, not_192_out);
  and and_78 (and_78_out, E1, E3, not_193_out, not_194_out, not_195_out);
  and and_79 (and_79_out, E1, not_196_out, E3, not_197_out, E6);
  and and_80 (and_80_out, E1, not_198_out, E3, E4, E5, not_199_out);
  and and_81 (and_81_out, E1, not_200_out, E3, E4, E5, not_201_out);
  and and_82 (and_82_out, E1, E2, not_202_out, not_203_out, E5);
  and and_83 (and_83_out, E1, E2, not_204_out, E5, E6);
  and and_84 (and_84_out, not_205_out, not_206_out, not_207_out, not_208_out, not_209_out);
  and and_85 (and_85_out, not_210_out, not_211_out, not_212_out);
  and and_86 (and_86_out, not_213_out, not_214_out, not_215_out);
  and and_87 (and_87_out, not_216_out, not_217_out, not_218_out);
  and and_88 (and_88_out, not_219_out, not_220_out, not_221_out, E6);
  and and_89 (and_89_out, not_222_out, not_223_out, E6, E7);
  and and_90 (and_90_out, not_224_out, E4, E5);
  and and_91 (and_91_out, E4, E5, E6);
  and and_92 (and_92_out, E3, not_225_out, not_226_out);
  and and_93 (and_93_out, not_227_out, not_228_out, E3, not_229_out, E7);
  and and_94 (and_94_out, not_230_out, E3, not_231_out, E6);
  and and_95 (and_95_out, E3, E4, E5, E7);
  and and_96 (and_96_out, E2, not_232_out, not_233_out, not_234_out, not_235_out);
  and and_97 (and_97_out, not_236_out, E2, not_237_out, E4);
  and and_98 (and_98_out, E2, E3, not_238_out, not_239_out);
  and and_99 (and_99_out, not_240_out, E2, E3, E5, not_241_out);
  and and_100 (and_100_out, E1, not_242_out, not_243_out, not_244_out);
  and and_101 (and_101_out, E1, not_245_out, not_246_out, not_247_out);
  and and_102 (and_102_out, E1, E2, not_248_out);
  and and_103 (and_103_out, not_249_out, not_250_out);
  and and_104 (and_104_out, not_251_out, not_252_out, not_253_out);
  and and_105 (and_105_out, not_254_out, not_255_out, E7);
  and and_106 (and_106_out, not_256_out, E6, E7);
  and and_107 (and_107_out, not_257_out, E5);
  and and_108 (and_108_out, not_258_out, E5, E6, E7);
  and and_109 (and_109_out, not_259_out, E3);
  and and_110 (and_110_out, not_260_out, E2, not_261_out);
  and and_111 (and_111_out, not_262_out, E2, not_263_out);
  and and_112 (and_112_out, E2, not_264_out, not_265_out);
  and and_113 (and_113_out, E1, not_266_out, E6);
  and and_114 (and_114_out, E1, E5, not_267_out);
  and and_115 (and_115_out, E1, E4, not_268_out);
  and and_116 (and_116_out, E1, E3, E4);
  or or_1 (S1, and_1_out, and_2_out, and_3_out, and_4_out, and_5_out, and_6_out, and_7_out, and_8_out, and_9_out, and_10_out, and_11_out, and_12_out);
  or or_2 (S3, and_32_out, and_33_out, and_34_out, and_35_out, and_36_out, and_37_out, and_38_out, and_39_out, and_40_out, and_41_out, and_42_out, and_43_out, and_44_out, and_45_out, and_46_out);
  or or_3 (S4, and_47_out, and_48_out, and_49_out, and_50_out, and_51_out, and_52_out, and_53_out, and_54_out, and_55_out, and_56_out, and_57_out, and_58_out, and_59_out, and_60_out, and_61_out);
  or or_4 (S6, and_84_out, and_85_out, and_86_out, and_87_out, and_88_out, and_89_out, and_90_out, and_91_out, and_92_out, and_93_out, and_94_out, and_95_out, and_96_out, and_97_out, and_98_out, and_99_out, and_100_out, and_101_out, and_102_out);
  or or_5 (S7, and_103_out, and_104_out, and_105_out, and_106_out, and_107_out, and_108_out, and_109_out, and_110_out, and_111_out, and_112_out, and_113_out, and_114_out, and_115_out, and_116_out);
  or or_6 (S2, and_13_out, and_14_out, and_15_out, and_16_out, and_17_out, and_18_out, and_19_out, and_20_out, and_21_out, and_22_out, and_23_out, and_24_out, and_25_out, and_26_out, and_27_out, and_28_out, and_29_out, and_30_out, and_31_out);
  or or_7 (S5, and_62_out, and_63_out, and_64_out, and_65_out, and_66_out, and_67_out, and_68_out, and_69_out, and_70_out, and_71_out, and_72_out, and_73_out, and_74_out, and_75_out, and_76_out, and_77_out, and_78_out, and_79_out, and_80_out, and_81_out, and_82_out, and_83_out);
endmodule

module Centenas (
  input  E1,
  input  E2,
  input  E3,
  input  E4,
  input  E5,
  input  E6,
  input  E7,
  input  E8,
  output S1,
  output S2,
  output S3,
  output S4,
  output S5,
  output S6,
  output S7
);

  wire and_1_out, and_2_out, and_3_out, and_4_out, and_5_out, and_6_out, and_7_out, and_8_out, and_9_out,
       and_10_out, and_11_out, and_12_out, and_13_out, and_14_out, and_15_out, and_16_out, and_17_out,
       and_18_out, and_19_out, and_20_out, and_21_out, and_22_out, and_23_out, and_24_out, and_25_out,
       not_1_out, not_2_out, not_3_out, not_4_out, not_5_out, not_6_out, not_7_out, not_8_out, not_9_out,
       not_10_out, not_11_out, not_12_out, not_13_out, not_14_out, not_15_out, not_16_out, not_17_out,
       not_18_out, not_19_out, not_20_out, not_21_out, not_22_out, not_23_out, not_24_out, not_25_out,
       not_26_out, not_27_out, not_28_out, not_29_out, not_30_out, not_31_out, not_32_out, not_33_out,
       not_34_out, not_35_out, not_36_out, not_37_out, not_38_out, not_39_out, not_40_out, not_41_out,
       not_42_out, not_43_out;

  and and_1 (and_1_out, E1, E2, E5);
  and and_2 (and_2_out, E1, E2, E4);
  and and_3 (and_3_out, E1, E2, E3);
  not not_1 (not_1_out, E1);
  not not_2 (not_2_out, E2);
  not not_3 (not_3_out, E1);
  not not_4 (not_4_out, E3);
  not not_5 (not_5_out, E1);
  not not_6 (not_6_out, E4);
  not not_7 (not_7_out, E5);
  not not_8 (not_8_out, E6);
  not not_9 (not_9_out, E1);
  not not_10 (not_10_out, E2);
  not not_11 (not_11_out, E1);
  not not_12 (not_12_out, E3);
  not not_13 (not_13_out, E1);
  not not_14 (not_14_out, E4);
  not not_15 (not_15_out, E5);
  not not_16 (not_16_out, E6);
  not not_17 (not_17_out, E3);
  not not_18 (not_18_out, E3);
  not not_19 (not_19_out, E1);
  not not_20 (not_20_out, E2);
  not not_21 (not_21_out, E1);
  not not_22 (not_22_out, E3);
  not not_23 (not_23_out, E1);
  not not_24 (not_24_out, E4);
  not not_25 (not_25_out, E5);
  not not_26 (not_26_out, E6);
  not not_27 (not_27_out, E3);
  not not_28 (not_28_out, E3);
  not not_29 (not_29_out, E1);
  not not_30 (not_30_out, E2);
  not not_31 (not_31_out, E1);
  not not_32 (not_32_out, E3);
  not not_33 (not_33_out, E1);
  not not_34 (not_34_out, E4);
  not not_35 (not_35_out, E5);
  not not_36 (not_36_out, E6);
  not not_37 (not_37_out, E3);
  not not_38 (not_38_out, E3);
  not not_39 (not_39_out, E1);
  not not_40 (not_40_out, E2);
  not not_41 (not_41_out, E3);
  and and_4 (and_4_out, not_41_out, not_42_out, not_43_out);
  not not_42 (not_42_out, E4);
  not not_43 (not_43_out, E5);
  or or_1 (S1, and_1_out, and_2_out, and_3_out);
  and and_5 (and_5_out, not_1_out, not_2_out);
  or or_2 (S2, and_5_out, and_6_out, and_7_out);
  and and_6 (and_6_out, not_3_out, not_4_out);
  and and_7 (and_7_out, not_5_out, not_6_out, not_7_out, not_8_out);
  and and_8 (and_8_out, not_9_out, not_10_out);
  and and_9 (and_9_out, not_11_out, not_12_out);
  and and_10 (and_10_out, not_13_out, not_14_out, not_15_out, not_16_out);
  and and_11 (and_11_out, E2, not_17_out, E5);
  and and_12 (and_12_out, E2, not_18_out, E4);
  and and_13 (and_13_out, E1, E2, E3);
  and and_14 (and_14_out, not_19_out, not_20_out);
  and and_15 (and_15_out, not_21_out, not_22_out);
  and and_16 (and_16_out, not_23_out, not_24_out, not_25_out, not_26_out);
  and and_17 (and_17_out, E2, not_27_out, E5);
  and and_18 (and_18_out, E2, not_28_out, E4);
  and and_19 (and_19_out, E1, E2, E3);
  and and_20 (and_20_out, not_29_out, not_30_out);
  and and_21 (and_21_out, not_31_out, not_32_out);
  and and_22 (and_22_out, not_33_out, not_34_out, not_35_out, not_36_out);
  and and_23 (and_23_out, E2, not_37_out, E5);
  and and_24 (and_24_out, E2, not_38_out, E4);
  and and_25 (and_25_out, E1, E2, E3);
  or or_3 (S7, not_39_out, not_40_out, and_4_out);
  or or_4 (S3, and_8_out, and_9_out, and_10_out, and_11_out, and_12_out, and_13_out);
  or or_5 (S5, and_14_out, and_15_out, and_16_out, and_17_out, and_18_out, and_19_out);
  or or_6 (S6, and_20_out, and_21_out, and_22_out, and_23_out, and_24_out, and_25_out);

  assign S4 = 1'b1;
endmodule
